// Logisim project 9-BIT D FLIP FLOP.circ as structural Verilog: 1 circuit, main circuit main
module main (
  input  CLK,
  input  EN,
  input  [9:0] INPUT,
  output [9:0] OUTPUT
);

  D_Flip_Flop d_ff_1 (.clk(CLK), .D(INPUT[0]), .Q(OUTPUT[9]), .en(EN));  // open: Qn, preset, reset
  D_Flip_Flop d_ff_2 (.clk(CLK), .D(INPUT[1]), .Q(OUTPUT[8]), .en(EN));  // open: Qn, preset, reset
  D_Flip_Flop d_ff_3 (.clk(CLK), .D(INPUT[2]), .Q(OUTPUT[7]), .en(EN));  // open: Qn, preset, reset
  D_Flip_Flop d_ff_4 (.clk(CLK), .D(INPUT[3]), .Q(OUTPUT[6]), .en(EN));  // open: Qn, preset, reset
  D_Flip_Flop d_ff_5 (.clk(CLK), .D(INPUT[4]), .Q(OUTPUT[5]), .en(EN));  // open: Qn, preset, reset
  D_Flip_Flop d_ff_6 (.clk(CLK), .D(INPUT[5]), .Q(OUTPUT[4]), .en(EN));  // open: Qn, preset, reset
  D_Flip_Flop d_ff_7 (.clk(CLK), .D(INPUT[6]), .Q(OUTPUT[3]), .en(EN));  // open: Qn, preset, reset
  D_Flip_Flop d_ff_8 (.clk(CLK), .D(INPUT[7]), .Q(OUTPUT[2]), .en(EN));  // open: Qn, preset, reset
  D_Flip_Flop d_ff_9 (.clk(CLK), .D(INPUT[8]), .Q(OUTPUT[1]), .en(EN));  // open: Qn, preset, reset
  D_Flip_Flop d_ff_10 (.clk(CLK), .D(INPUT[9]), .Q(OUTPUT[0]), .en(EN));  // open: Qn, preset, reset
endmodule
