// Logisim project ADDER - 16 BIT.circ as structural Verilog: 1 circuit, main circuit main
module main (
  input  [15:0] INPUT_1,
  input  [15:0] INPUT_2,
  output [15:0] OUTPUT
);

  wire adder_1_cout, adder_2_cout, adder_3_cout, adder_4_cout, adder_5_cout, adder_6_cout, adder_7_cout,
       adder_8_cout, adder_9_cout, adder_10_cout, adder_11_cout, adder_12_cout, adder_13_cout, adder_14_cout,
       adder_15_cout;

  Adder #(.width(1)) adder_1 (.a(INPUT_1[0]), .b(INPUT_2[0]), .out(OUTPUT[0]), .cout(adder_1_cout));  // open: cin
  Adder #(.width(1)) adder_2 (.a(INPUT_1[1]), .b(INPUT_2[1]), .out(OUTPUT[1]), .cin(adder_1_cout), .cout(adder_2_cout));
  Adder #(.width(1)) adder_3 (.a(INPUT_1[2]), .b(INPUT_2[2]), .out(OUTPUT[2]), .cin(adder_2_cout), .cout(adder_3_cout));
  Adder #(.width(1)) adder_4 (.a(INPUT_1[3]), .b(INPUT_2[3]), .out(OUTPUT[3]), .cin(adder_3_cout), .cout(adder_4_cout));
  Adder #(.width(1)) adder_5 (.a(INPUT_1[4]), .b(INPUT_2[4]), .out(OUTPUT[4]), .cin(adder_4_cout), .cout(adder_5_cout));
  Adder #(.width(1)) adder_6 (.a(INPUT_1[5]), .b(INPUT_2[5]), .out(OUTPUT[5]), .cin(adder_5_cout), .cout(adder_6_cout));
  Adder #(.width(1)) adder_7 (.a(INPUT_1[6]), .b(INPUT_2[6]), .out(OUTPUT[6]), .cin(adder_6_cout), .cout(adder_7_cout));
  Adder #(.width(1)) adder_8 (.a(INPUT_1[7]), .b(INPUT_2[7]), .out(OUTPUT[7]), .cin(adder_7_cout), .cout(adder_8_cout));
  Adder #(.width(1)) adder_9 (.a(INPUT_1[8]), .b(INPUT_2[8]), .out(OUTPUT[8]), .cin(adder_8_cout), .cout(adder_9_cout));
  Adder #(.width(1)) adder_10 (
    .a(INPUT_1[9]), .b(INPUT_2[9]), .out(OUTPUT[9]), .cin(adder_9_cout), .cout(adder_10_cout));
  Adder #(.width(1)) adder_11 (
    .a(INPUT_1[10]), .b(INPUT_2[10]), .out(OUTPUT[10]), .cin(adder_10_cout), .cout(adder_11_cout));
  Adder #(.width(1)) adder_12 (
    .a(INPUT_1[11]), .b(INPUT_2[11]), .out(OUTPUT[11]), .cin(adder_11_cout), .cout(adder_12_cout));
  Adder #(.width(1)) adder_13 (
    .a(INPUT_1[12]), .b(INPUT_2[12]), .out(OUTPUT[12]), .cin(adder_12_cout), .cout(adder_13_cout));
  Adder #(.width(1)) adder_14 (
    .a(INPUT_1[13]), .b(INPUT_2[13]), .out(OUTPUT[13]), .cin(adder_13_cout), .cout(adder_14_cout));
  Adder #(.width(1)) adder_15 (
    .a(INPUT_1[14]), .b(INPUT_2[14]), .out(OUTPUT[14]), .cin(adder_14_cout), .cout(adder_15_cout));
  Adder #(.width(1)) adder_16 (.a(INPUT_1[15]), .b(INPUT_2[15]), .out(OUTPUT[15]), .cin(adder_15_cout));  // open: cout
endmodule
