// Logisim project ADDER - 8 BIT.circ as structural Verilog: 1 circuit, main circuit main
module main (
  input  [7:0] Input_1,
  input  [7:0] Input_2,
  output [7:0] Output
);

  wire adder_1_cout, adder_2_cout, adder_3_cout, adder_4_cout, adder_5_cout, adder_6_cout, adder_7_cout;

  Adder #(.width(1)) adder_1 (.a(Input_2[0]), .b(Input_1[0]), .out(Output[0]), .cout(adder_1_cout));  // open: cin
  Adder #(.width(1)) adder_2 (.a(Input_2[1]), .b(Input_1[1]), .out(Output[1]), .cin(adder_1_cout), .cout(adder_2_cout));
  Adder #(.width(1)) adder_3 (.a(Input_2[2]), .b(Input_1[2]), .out(Output[2]), .cin(adder_2_cout), .cout(adder_3_cout));
  Adder #(.width(1)) adder_4 (.a(Input_2[3]), .b(Input_1[3]), .out(Output[3]), .cin(adder_3_cout), .cout(adder_4_cout));
  Adder #(.width(1)) adder_5 (.a(Input_2[4]), .b(Input_1[4]), .out(Output[4]), .cin(adder_4_cout), .cout(adder_5_cout));
  Adder #(.width(1)) adder_6 (.a(Input_2[5]), .b(Input_1[5]), .out(Output[5]), .cin(adder_5_cout), .cout(adder_6_cout));
  Adder #(.width(1)) adder_7 (.a(Input_2[6]), .b(Input_1[6]), .out(Output[6]), .cin(adder_6_cout), .cout(adder_7_cout));
  Adder #(.width(1)) adder_8 (.a(Input_2[7]), .b(Input_1[7]), .out(Output[7]), .cin(adder_7_cout));  // open: cout
endmodule
