// Logisim project ALU_update.circ as structural Verilog: 1 circuit, main circuit main
module main (
  input  [7:0] A,
  input  [7:0] B,
  input  Cin,
  input  [3:0] Funsel,
  output [7:0] OutALU,
  output [3:0] flags_enable,
  output [3:0] OutFlag__ZCNO
);

  wire main_1_cout, main_1_overflow, main_2_csl_carry, main_2_csl_ovflw, main_2_csr_carry, main_2_csr_oflw,
       main_2_lsl_carry, main_2_ovflw, multiplexer_3_out, multiplexer_4_out, multiplexer_5_out;
  wire [7:0] and_1_out, main_1_output, main_2_asl, main_2_asr, main_2_csl, main_2_csr, main_2_lsl,
       main_2_lsr, not_1_out, not_2_out, or_1_out, xor_1_out;

  assign not_1_out = ~A;  // NOT_Gate not_1, 8 bits wide
  assign and_1_out = A & B;  // AND_Gate and_1, 8 bits wide
  assign or_1_out = A | B;  // OR_Gate or_1, 8 bits wide
  assign xor_1_out = B ^ A;  // XOR_Gate xor_1, 8 bits wide
  assign not_2_out = ~B;  // NOT_Gate not_2, 8 bits wide
  adder_main main_1 (
    .A(A), .B(B), .Funsel_last2(Funsel[1:0]), .Cin(Cin), .Cout(main_1_cout), .Output(main_1_output),
    .Overflow(main_1_overflow));
  Shifters_main main_2 (
    .IN(A), .C(Cin), .OVFLW(main_2_ovflw), .LSL(main_2_lsl), .LSR(main_2_lsr), .ASL(main_2_asl),
    .ASR(main_2_asr), .CSL(main_2_csl), .CSR(main_2_csr), .LSL_CARRY(main_2_lsl_carry),
    .CSR_OFLW(main_2_csr_oflw), .CSL_OVFLW(main_2_csl_ovflw), .CSL_CARRY(main_2_csl_carry),
    .CSR_CARRY(main_2_csr_carry));  // open: CARRY, LSR_CARRY
  Multiplexer #(.enable("false")) multiplexer_1 (
    .in0(main_1_overflow), .in1(multiplexer_3_out), .out(OutFlag__ZCNO[3]), .sel(Funsel[3]));
  Multiplexer #(.enable("false")) multiplexer_2 (
    .in0(main_1_cout), .in1(multiplexer_5_out), .out(OutFlag__ZCNO[1]), .sel(Funsel[3]));
  Multiplexer #(.select(2), .enable("false")) multiplexer_3 (
    .in0(1'b0), .in1(main_2_ovflw), .in2(main_2_csl_ovflw), .in3(main_2_csr_oflw), .out(multiplexer_3_out),
    .sel(Funsel[1:0]));
  Multiplexer #(.enable("false")) multiplexer_4 (
    .in0(main_2_csl_carry), .in1(main_2_csr_carry), .out(multiplexer_4_out), .sel(Funsel[0]));
  Multiplexer #(.enable("false")) multiplexer_5 (
    .in0(main_2_lsl_carry), .in1(multiplexer_4_out), .out(multiplexer_5_out), .sel(Funsel[2]));
  Multiplexer #(.select(4), .width(8), .enable("false")) multiplexer_6 (
    .in0(A), .in1(B), .in2(not_1_out), .in3(not_2_out), .in4(main_1_output), .in5(main_1_output),
    .in6(main_1_output), .in7(and_1_out), .in8(or_1_out), .in9(xor_1_out), .in10(main_2_lsl),
    .in11(main_2_lsr), .in12(main_2_asl), .in13(main_2_asr), .in14(main_2_csl), .in15(main_2_csr),
    .out(OutALU), .sel(Funsel));
  nor nor_1 (OutFlag__ZCNO[0], OutALU[0], OutALU[1], OutALU[2], OutALU[3], OutALU[4], OutALU[5], OutALU[6], OutALU[7]);
  Multiplexer #(.select(4), .width(4), .enable("false")) multiplexer_7 (
    .in0(4'b0101), .in1(4'b0101), .in2(4'b0101), .in3(4'b0101), .in4(4'b1111), .in5(4'b1111), .in6(4'b1111),
    .in7(4'b0101), .in8(4'b0101), .in9(4'b0101), .in10(4'b0111), .in11(4'b0101), .in12(4'b0101),
    .in13(4'b1001), .in14(4'b1111), .in15(4'b1111), .out(flags_enable), .sel(Funsel));

  assign OutFlag__ZCNO[2] = OutALU[7];
endmodule
