// Logisim project ArithmeticShift.circ as structural Verilog: 1 circuit, main circuit main
module main (
  input  [7:0] IN,
  output ASL_OVERFLOW,
  output [7:0] ASL,
  output [7:0] ASR
);

  Shifter shifter_1 (.in(IN), .\dist (3'b001), .out(ASL));
  Shifter #(.shift("ar")) shifter_2 (.in(IN), .\dist (3'b001), .out(ASR));
  xor xor_1 (ASL_OVERFLOW, IN[6], IN[7]);
endmodule
