// Logisim project CU (serhat).circ as structural Verilog: 1 circuit, main circuit OUTASEL
module OUTASEL (
  input  Z,
  input  [15:0] INSTRUCTION,
  input  rewind,
  input  CLK,
  input  [1:0] OUTASEL,
  input  [1:0] OUTBSEL,
  input  [1:0] deletethis,
  input  [1:0] deletethis_2,
  input  [1:0] OUTCSEL,
  input  [1:0] deletethis_3,
  input  [1:0] deletethis_4,
  output [1:0] deneme
);

  wire and_1_out, and_2_out, and_3_out, and_4_out, and_5_out, and_6_out, and_7_out, and_8_out, and_9_out,
       and_10_out, and_11_out, and_12_out, and_13_out, and_14_out, and_15_out, and_16_out, and_17_out,
       and_18_out, and_19_out, and_20_out, and_21_out, and_22_out, and_23_out, and_24_out, and_25_out,
       and_26_out, and_27_out, and_28_out, and_29_out, and_30_out, and_31_out, and_32_out, and_33_out,
       and_34_out, and_35_out, and_36_out, and_37_out, and_38_out, d_ff_1_q, not_1_out, not_2_out, not_3_out,
       not_4_out, not_5_out, not_6_out, not_8_out, not_9_out, not_12_out, not_13_out, not_14_out, not_15_out,
       not_16_out, not_17_out, not_18_out, not_19_out, not_20_out, not_21_out, not_22_out, not_23_out,
       not_24_out, not_25_out, not_26_out, not_27_out, not_28_out, not_29_out, not_30_out, not_31_out,
       not_32_out, not_33_out, not_34_out, not_35_out, not_36_out, Opcode0, Opcode1, Opcode2, Opcode3,
       Opcode4, Opcode5, Opcode6, Opcode7, Opcode8, Opcode9, Opcode10, Opcode11, Opcode12, Opcode13,
       Opcode14, Opcode15, Opcode16, Opcode17, Opcode18, Opcode19, or_1_out, or_2_out, or_3_out, or_4_out,
       or_5_out, or_6_out, or_7_out, or_8_out, or_9_out, or_10_out, or_11_out, or_12_out, or_13_out,
       or_14_out, or_15_out, or_16_out, or_17_out, or_18_out, or_19_out, or_20_out, or_21_out, or_22_out,
       or_23_out, or_24_out, or_25_out, T0, T1, T2, T3, T4, T5, T6, T7;
  wire [2:0] counter_1_q;
  wire [3:0] DESTREG_2A_2, DESTREG_2B_2, REGSEL_2A_0, SRCREG1_2A_2, SRCREG1_2B_2, SRCREG2_2A_2, SRCREG2_2B_2;

  Counter #(.width(3), .max('h7)) counter_1 (
    .count(1'b1), .Q(counter_1_q), .clk(CLK), .clr(d_ff_1_q));  // open: load, D, carry
  D_Flip_Flop d_ff_1 (.clk(CLK), .D(rewind), .Q(d_ff_1_q), .en(1'b1), .reset(d_ff_1_q));  // open: Qn, preset
  not not_1 (not_1_out, INSTRUCTION[5]);
  Decoder #(.select(3), .enable("false")) decoder_1 (
    .out0(T0), .out1(T1), .out2(T2), .out3(T3), .out4(T4), .out5(T5), .out6(T6), .out7(T7), .sel(counter_1_q));
  Decoder #(.select(2)) decoder_2 (
    .out0(SRCREG2_2A_2[3]), .out1(SRCREG2_2A_2[1]), .out2(SRCREG2_2A_2[2]), .out3(SRCREG2_2A_2[0]),
    .sel(INSTRUCTION[4:3]), .en(not_1_out));
  Decoder #(.select(2)) decoder_3 (
    .out0(SRCREG2_2B_2[3]), .out1(SRCREG2_2B_2[2]), .out2(SRCREG2_2B_2[1]), .out3(SRCREG2_2B_2[0]),
    .sel(INSTRUCTION[4:3]), .en(INSTRUCTION[5]));
  Decoder #(.select(5), .enable("false")) decoder_4 (
    .out0(Opcode0), .out1(Opcode1), .out2(Opcode2), .out3(Opcode3), .out4(Opcode4), .out5(Opcode5),
    .out6(Opcode6), .out7(Opcode7), .out8(Opcode8), .out9(Opcode9), .out10(Opcode10), .out11(Opcode11),
    .out12(Opcode12), .out13(Opcode13), .out14(Opcode14), .out15(Opcode15), .out16(Opcode16),
    .out17(Opcode17), .out18(Opcode18), .out19(Opcode19), .sel(INSTRUCTION[15:11]));  // open: out20, out21, out22, out23, out24, out25, out26, out27, out28, out29, out30, out31
  Decoder #(.select(2), .enable("false")) decoder_5 (
    .out0(REGSEL_2A_0[0]), .out1(REGSEL_2A_0[1]), .out2(REGSEL_2A_0[2]), .out3(REGSEL_2A_0[3]),
    .sel(INSTRUCTION[10:9]));
  not not_2 (not_2_out, INSTRUCTION[10]);
  not not_3 (not_3_out, INSTRUCTION[2]);
  Decoder #(.select(2)) decoder_6 (
    .out0(DESTREG_2A_2[3]), .out1(DESTREG_2A_2[1]), .out2(DESTREG_2A_2[2]), .out3(DESTREG_2A_2[0]),
    .sel(INSTRUCTION[9:8]), .en(not_2_out));
  Decoder #(.select(2)) decoder_7 (
    .out0(DESTREG_2B_2[3]), .out1(DESTREG_2B_2[2]), .out2(DESTREG_2B_2[1]), .out3(DESTREG_2B_2[0]),
    .sel(INSTRUCTION[9:8]), .en(INSTRUCTION[10]));
  Decoder #(.select(2)) decoder_8 (
    .out0(SRCREG1_2A_2[3]), .out1(SRCREG1_2A_2[1]), .out2(SRCREG1_2A_2[2]), .out3(SRCREG1_2A_2[0]),
    .sel(INSTRUCTION[1:0]), .en(not_3_out));
  Decoder #(.select(2)) decoder_9 (
    .out0(SRCREG1_2B_2[3]), .out1(SRCREG1_2B_2[2]), .out2(SRCREG1_2B_2[1]), .out3(SRCREG1_2B_2[0]),
    .sel(INSTRUCTION[1:0]), .en(INSTRUCTION[2]));
  not not_4 (not_4_out, INSTRUCTION[5]);
  and and_1 (and_1_out, T4, Opcode0);
  and and_2 (and_2_out, T4, Opcode4);
  and and_3 (and_3_out, T3, Opcode14);
  and and_4 (and_4_out, T3, INSTRUCTION[5], Opcode2);
  buf or_1 (or_1_out, and_4_out);  // OR_Gate
  and and_5 (and_5_out, T3, not_4_out, Opcode2);
  or or_2 (or_2_out, and_1_out, and_2_out);
  buf or_3 (or_3_out, and_3_out);  // OR_Gate
  assign deneme = or_3_out ? 2'b00 : 2'bz;  // Controlled_Buffer controlled_buffer_1
  assign deneme = or_1_out ? 2'b10 : 2'bz;  // Controlled_Buffer controlled_buffer_2
  buf or_4 (or_4_out, and_5_out);  // OR_Gate
  assign deneme = or_2_out ? 2'b01 : 2'bz;  // Controlled_Buffer controlled_buffer_3
  assign deneme = or_4_out ? 2'b11 : 2'bz;  // Controlled_Buffer controlled_buffer_4
  not not_5 (not_5_out, INSTRUCTION[8]);
  not not_6 (not_6_out, INSTRUCTION[8]);
  not not_7 (Opcode5, INSTRUCTION[4]);
  not not_8 (not_8_out, INSTRUCTION[10]);
  not not_9 (not_9_out, INSTRUCTION[10]);
  not not_10 (Opcode8, INSTRUCTION[7]);
  or or_5 (or_5_out, Opcode9, Opcode10);
  or or_6 (or_6_out, Opcode11, Opcode12, Opcode13);
  and and_6 (and_6_out, not_5_out, Opcode0, T5);
  and and_7 (and_7_out, INSTRUCTION[8], Opcode0, T4);
  and and_8 (and_8_out, Opcode1, T4);
  and and_9 (and_9_out, not_9_out, Opcode8, Opcode8, T6);
  not not_11 (Opcode5, INSTRUCTION[7]);
  not not_12 (not_12_out, INSTRUCTION[4]);
  not not_13 (not_13_out, INSTRUCTION[7]);
  not not_14 (not_14_out, INSTRUCTION[7]);
  and and_10 (and_10_out, not_6_out, Opcode5, Opcode5, T4);
  and and_11 (and_11_out, not_8_out, Opcode7, Opcode7, T6);
  not not_15 (not_15_out, INSTRUCTION[4]);
  and and_12 (and_12_out, not_12_out, not_13_out, or_5_out, T4);
  and and_13 (and_13_out, not_14_out, or_6_out, T4);
  or or_7 (or_7_out, and_6_out, and_7_out, and_8_out);
  or or_8 (or_8_out, and_10_out, and_11_out, and_9_out);
  and and_14 (and_14_out, not_15_out, Opcode5, Opcode5, T4);
  or or_9 (or_9_out, and_12_out, and_13_out);
  assign OUTASEL = or_7_out ? {INSTRUCTION[9], INSTRUCTION[10]} : 2'bz;  // Controlled_Buffer controlled_buffer_5
  assign OUTASEL = or_8_out ? {INSTRUCTION[5], INSTRUCTION[6]} : 2'bz;  // Controlled_Buffer controlled_buffer_6
  assign OUTASEL = and_14_out ? SRCREG2_2A_2[1:0] : 2'bz;  // Controlled_Buffer controlled_buffer_7
  assign OUTASEL = or_9_out ? SRCREG1_2A_2[1:0] : 2'bz;  // Controlled_Buffer controlled_buffer_8
  not not_16 (not_16_out, INSTRUCTION[4]);
  not not_17 (not_17_out, INSTRUCTION[4]);
  not not_18 (not_18_out, INSTRUCTION[7]);
  or or_10 (or_10_out, Opcode9, Opcode10);
  not not_19 (not_19_out, INSTRUCTION[4]);
  not not_20 (not_20_out, INSTRUCTION[7]);
  or or_11 (or_11_out, Opcode9, Opcode10);
  not not_21 (not_21_out, INSTRUCTION[4]);
  or or_12 (or_12_out, Opcode9, Opcode10);
  not not_22 (not_22_out, INSTRUCTION[7]);
  not not_23 (not_23_out, INSTRUCTION[10]);
  and and_15 (and_15_out, T4, not_17_out, Opcode5);
  and and_16 (and_16_out, T4, not_18_out, Opcode6);
  not not_24 (not_24_out, INSTRUCTION[10]);
  not not_25 (not_25_out, INSTRUCTION[7]);
  or or_13 (or_13_out, Opcode2, Opcode7, Opcode8);
  not not_26 (not_26_out, INSTRUCTION[4]);
  not not_27 (not_27_out, INSTRUCTION[7]);
  not not_28 (not_28_out, INSTRUCTION[7]);
  and and_17 (and_17_out, T4, not_19_out, not_20_out, or_11_out);
  and and_18 (and_18_out, T4, not_22_out, Opcode5);
  and and_19 (and_19_out, T4, not_16_out, Opcode5);
  and and_20 (and_20_out, T5, not_24_out, INSTRUCTION[7], Opcode5);
  and and_21 (and_21_out, T4, not_28_out, or_10_out);
  and and_22 (and_22_out, T4, INSTRUCTION[7], not_21_out, or_12_out);
  or or_14 (or_14_out, and_18_out, and_19_out);
  or or_15 (or_15_out, and_15_out, and_16_out);
  assign OUTBSEL = or_15_out ? {INSTRUCTION[5], INSTRUCTION[6]} : 2'bz;  // Controlled_Buffer controlled_buffer_9
  assign OUTBSEL = and_20_out ? {INSTRUCTION[9], INSTRUCTION[10]} : 2'bz;  // Controlled_Buffer controlled_buffer_10
  and and_23 (and_23_out, T4, not_25_out, or_13_out);
  and and_24 (and_24_out, T4, not_27_out, Opcode6);
  or or_16 (or_16_out, and_17_out, and_22_out);
  assign OUTBSEL = or_14_out ? {INSTRUCTION[2], INSTRUCTION[3]} : 2'bz;  // Controlled_Buffer controlled_buffer_11
  or or_17 (or_17_out, and_23_out, and_24_out, and_21_out);
  assign OUTBSEL = or_17_out ? SRCREG1_2A_2[1:0] : 2'bz;  // Controlled_Buffer controlled_buffer_12
  assign OUTBSEL = or_16_out ? SRCREG2_2A_2[1:0] : 2'bz;  // Controlled_Buffer controlled_buffer_13
  not not_29 (not_29_out, INSTRUCTION[7]);
  not not_30 (not_30_out, INSTRUCTION[7]);
  not not_31 (not_31_out, INSTRUCTION[10]);
  not not_32 (not_32_out, INSTRUCTION[7]);
  not not_33 (not_33_out, INSTRUCTION[10]);
  not not_34 (not_34_out, INSTRUCTION[4]);
  not not_35 (not_35_out, INSTRUCTION[4]);
  not not_36 (not_36_out, INSTRUCTION[4]);
  or or_18 (or_18_out, Opcode8, Opcode7);
  or or_19 (or_19_out, Opcode9, Opcode10);
  or or_20 (or_20_out, Opcode9, Opcode10);
  or or_21 (or_21_out, Opcode11, Opcode12, Opcode13);
  and and_25 (and_25_out, T4, INSTRUCTION[4], not_29_out, INSTRUCTION[10], Opcode6);
  and and_26 (and_26_out, T4, INSTRUCTION[7], or_18_out);
  and and_27 (and_27_out, T4, INSTRUCTION[4], not_30_out, or_19_out);
  and and_28 (and_28_out, T5, INSTRUCTION[4], INSTRUCTION[7], not_31_out, Opcode5);
  and and_29 (and_29_out, T6, INSTRUCTION[10], Opcode7);
  and and_30 (and_30_out, T6, INSTRUCTION[7], Opcode8);
  and and_31 (and_31_out, T6, INSTRUCTION[10], not_32_out, Opcode8);
  and and_32 (and_32_out, T4, Opcode17);
  and and_33 (and_33_out, T4, INSTRUCTION[7], Opcode2);
  and and_34 (and_34_out, T4, INSTRUCTION[4], not_33_out, Opcode5);
  and and_35 (and_35_out, T4, not_34_out, INSTRUCTION[7], Opcode5);
  and and_36 (and_36_out, T4, not_35_out, INSTRUCTION[7], INSTRUCTION[10], Opcode6);
  and and_37 (and_37_out, T4, not_36_out, INSTRUCTION[7], or_20_out);
  and and_38 (and_38_out, T4, INSTRUCTION[7], or_21_out);
  or or_22 (or_22_out, and_29_out, and_30_out, and_31_out);
  or or_23 (or_23_out, and_32_out, T0, T1, T2);
  or or_24 (or_24_out, and_33_out, and_34_out, and_35_out, and_36_out, and_37_out, and_38_out);
  or or_25 (or_25_out, and_25_out, and_26_out, and_27_out, and_28_out);
  assign OUTCSEL = or_22_out ? DESTREG_2B_2[1:0] : 2'bz;  // Controlled_Buffer controlled_buffer_14
  assign OUTCSEL = or_25_out ? SRCREG2_2B_2[1:0] : 2'bz;  // Controlled_Buffer controlled_buffer_15
  assign OUTCSEL = or_23_out ? 2'b00 : 2'bz;  // Controlled_Buffer controlled_buffer_16
  assign OUTCSEL = or_24_out ? SRCREG1_2B_2[1:0] : 2'bz;  // Controlled_Buffer controlled_buffer_17

  // Other names for the same wires on the sheet: IR4 = INSTRUCTION[4]; IR11 = INSTRUCTION[11]; IR12 = INSTRUCTION[12];
  //   IR13 = INSTRUCTION[13]; IR14 = INSTRUCTION[14]; IR15 = INSTRUCTION[15]; IR0 = INSTRUCTION[0];
  //   IR1 = INSTRUCTION[1]; IR8 = INSTRUCTION[8]; IR6 = INSTRUCTION[6]; IR5 = INSTRUCTION[5]; IR10 = INSTRUCTION[10];
  //   IR9 = INSTRUCTION[9]; IR3 = INSTRUCTION[3]; IR2 = INSTRUCTION[2]; IR7 = INSTRUCTION[7]

  // Notes on the sheet:
  //   Opcode
  //   okay eklerim onu da
  //   MUXASEL
  //   OUTASEL
  //   OUTBSEL
  //   OUTCSEL
endmodule
