// Logisim project CU_updated_last.circ as structural Verilog: 1 circuit, main circuit main
module main (
  input  Z,
  input  [15:0] INSTRUCTION,
  input  CLK,
  output Read,
  output Load,
  output EnableRam,
  output Enable_2C,
  output [1:0] OutDSel,
  output L_H,
  output [1:0] FunSel_2C,
  output [1:0] MuxBSel,
  output MuxCSel,
  output MuxBSelEnable,
  output MuxCSelEnable,
  output [1:0] FunSel2B,
  output MuxASelEnable,
  output [1:0] MuxASel,
  output [1:0] FunSel2A,
  output [1:0] OUTASEL,
  output [1:0] OUTBSEL,
  output [3:0] RegSel_2A,
  output [3:0] FunSel_ALU,
  output Enable_2A,
  output [1:0] OUTCSEL,
  output [2:0] RegSel_2B,
  output Enable_2B
);

  wire and_1_out, and_2_out, and_3_out, and_4_out, and_5_out, and_6_out, and_7_out, and_8_out, and_9_out,
       and_10_out, and_11_out, and_12_out, and_13_out, and_14_out, and_15_out, and_16_out, and_17_out,
       and_18_out, and_19_out, and_20_out, and_21_out, and_22_out, and_23_out, and_24_out, and_25_out,
       and_26_out, and_27_out, and_28_out, and_29_out, and_30_out, and_31_out, and_32_out, and_33_out,
       and_34_out, and_35_out, and_36_out, and_37_out, and_38_out, and_39_out, and_40_out, and_41_out,
       and_42_out, and_43_out, and_44_out, and_45_out, and_46_out, and_47_out, and_48_out, and_49_out,
       and_50_out, and_51_out, and_52_out, and_53_out, and_54_out, and_55_out, and_56_out, and_57_out,
       and_58_out, and_59_out, and_60_out, and_61_out, and_62_out, and_63_out, and_64_out, and_65_out,
       and_66_out, and_67_out, and_68_out, and_69_out, and_70_out, and_71_out, and_72_out, and_73_out,
       and_74_out, and_75_out, and_76_out, and_77_out, and_78_out, and_79_out, and_80_out, and_81_out,
       and_82_out, and_83_out, and_84_out, and_85_out, and_86_out, and_87_out, and_88_out, and_89_out,
       and_90_out, and_91_out, and_92_out, and_93_out, and_94_out, and_95_out, and_96_out, and_97_out,
       and_98_out, and_99_out, and_100_out, and_101_out, and_102_out, and_103_out, and_104_out, and_105_out,
       and_106_out, and_107_out, and_108_out, and_109_out, and_110_out, and_111_out, and_112_out,
       and_113_out, and_114_out, and_115_out, and_116_out, and_117_out, and_118_out, and_119_out,
       and_120_out, and_121_out, and_122_out, and_123_out, and_124_out, and_125_out, and_126_out,
       and_127_out, and_128_out, and_129_out, and_130_out, and_131_out, and_132_out, and_133_out,
       and_134_out, and_135_out, and_136_out, and_137_out, and_138_out, and_139_out, and_140_out,
       and_141_out, and_142_out, and_143_out, and_144_out, and_145_out, and_146_out, and_147_out,
       and_148_out, and_149_out, and_150_out, and_152_out, and_153_out, and_154_out, and_155_out,
       and_156_out, and_157_out, and_158_out, and_159_out, and_160_out, and_161_out, and_162_out,
       and_163_out, and_164_out, and_165_out, and_166_out, and_167_out, and_168_out, and_169_out,
       and_170_out, and_171_out, and_172_out, and_173_out, and_174_out, and_175_out, and_176_out,
       and_177_out, and_178_out, and_179_out, and_180_out, and_181_out, and_182_out, and_183_out,
       and_184_out, and_185_out, and_186_out, and_187_out, and_188_out, and_189_out, and_190_out,
       and_191_out, and_192_out, and_193_out, and_194_out, and_195_out, and_196_out, and_197_out,
       and_198_out, and_199_out, and_200_out, and_201_out, and_202_out, and_203_out, and_204_out,
       and_205_out, and_206_out, and_207_out, and_208_out, and_209_out, and_210_out, and_211_out,
       and_212_out, and_213_out, d_ff_1_q, decoder_3_out0, decoder_3_out1, decoder_6_out0, decoder_6_out1,
       decoder_8_out0, decoder_8_out1, IR17, not_1_out, not_2_out, not_3_out, not_5_out, not_6_out,
       not_7_out, not_8_out, not_9_out, not_10_out, not_11_out, not_12_out, not_13_out, not_14_out,
       not_15_out, not_16_out, not_17_out, not_18_out, not_19_out, not_20_out, not_21_out, not_22_out,
       not_23_out, not_24_out, not_25_out, not_26_out, not_27_out, not_28_out, not_29_out, not_30_out,
       not_31_out, not_32_out, not_33_out, not_34_out, not_35_out, not_36_out, not_37_out, not_38_out,
       not_39_out, not_40_out, not_41_out, not_42_out, not_43_out, not_44_out, not_45_out, not_46_out,
       not_47_out, not_48_out, not_49_out, not_50_out, not_51_out, not_52_out, not_53_out, not_54_out,
       not_55_out, not_56_out, not_57_out, not_58_out, not_59_out, not_60_out, not_61_out, not_62_out,
       not_63_out, not_64_out, not_65_out, not_66_out, not_67_out, not_68_out, not_69_out, not_70_out,
       not_71_out, not_72_out, not_73_out, not_74_out, not_75_out, not_76_out, not_77_out, not_78_out,
       not_79_out, not_80_out, not_81_out, not_82_out, not_83_out, not_84_out, not_85_out, not_86_out,
       not_87_out, not_88_out, not_89_out, not_90_out, not_91_out, not_92_out, not_93_out, not_94_out,
       not_95_out, not_96_out, not_97_out, not_98_out, not_99_out, not_100_out, not_101_out, not_102_out,
       not_103_out, not_104_out, not_105_out, not_106_out, not_107_out, not_108_out, not_109_out,
       not_110_out, not_111_out, not_112_out, not_113_out, not_114_out, not_115_out, not_116_out,
       not_117_out, not_118_out, not_119_out, not_120_out, not_121_out, not_122_out, not_123_out,
       not_124_out, not_125_out, not_126_out, not_127_out, not_128_out, not_129_out, not_130_out,
       not_131_out, not_132_out, not_133_out, not_134_out, not_135_out, not_136_out, not_137_out,
       not_138_out, not_139_out, not_140_out, not_141_out, not_142_out, not_143_out, not_144_out,
       not_145_out, not_146_out, not_147_out, not_148_out, not_149_out, not_150_out, not_151_out,
       not_152_out, not_153_out, not_154_out, not_155_out, not_156_out, not_157_out, not_158_out,
       not_159_out, not_160_out, not_161_out, not_162_out, not_163_out, not_164_out, not_165_out,
       not_166_out, not_167_out, not_168_out, not_169_out, not_170_out, not_171_out, not_172_out,
       not_173_out, not_174_out, not_175_out, not_176_out, not_177_out, not_178_out, not_179_out,
       not_180_out, not_181_out, not_182_out, not_183_out, not_184_out, not_185_out, not_186_out,
       not_187_out, not_188_out, not_189_out, not_190_out, not_191_out, not_192_out, not_193_out,
       not_194_out, not_195_out, not_196_out, Opcode0, Opcode1, Opcode2, Opcode2_Opcode7_Opcode8, Opcode3,
       Opcode4, Opcode5, Opcode5_Opcode9_Opcode10, Opcode6, Opcode6_Opcode9_Opcode10, Opcode7,
       Opcode7_Opcode8, Opcode8, Opcode9, Opcode10, Opcode11, Opcode11_Opcode12_Opcode13, Opcode12, Opcode13,
       Opcode14, Opcode15, Opcode16, Opcode17, Opcode18, Opcode_2_7, Opcode_2_7_8, Opcode_2_7_8_11_12_13,
       Opcode_9_10, Opcode_9_10_17, Opcode_11_12_13, or_4_out, or_5_out, or_6_out, or_17_out, or_20_out,
       or_21_out, or_23_out, or_24_out, or_25_out, or_26_out, or_27_out, or_28_out, or_29_out, or_30_out,
       or_31_out, or_32_out, or_33_out, or_34_out, or_35_out, or_36_out, or_37_out, or_38_out, or_39_out,
       or_40_out, or_41_out, or_42_out, or_43_out, or_44_out, or_45_out, or_46_out, or_47_out, or_48_out,
       or_49_out, or_50_out, or_51_out, or_52_out, or_53_out, or_54_out, or_55_out, or_56_out, or_57_out,
       or_58_out, or_59_out, or_60_out, or_61_out, or_62_out, or_63_out, or_64_out, or_65_out, or_67_out,
       or_68_out, or_70_out, or_71_out, or_72_out, or_73_out, or_74_out, or_75_out, or_76_out, or_78_out,
       or_79_out, or_80_out, or_81_out, or_82_out, or_83_out, or_85_out, or_86_out, or_87_out, or_88_out,
       or_89_out, or_91_out, or_92_out, or_93_out, or_94_out, or_95_out, or_96_out, or_97_out, or_98_out,
       Rewind, T0, T1, T2, T3, T4, T5, T6, T7, xor_1_out, xor_2_out, xor_3_out, xor_4_out;
  wire [2:0] counter_1_q, DESTREG_2B_2, SRCREG1_2B_2, SRCREG2_2B_2;
  wire [3:0] DESTREG_2A_2, DESTREG_2A_2_t, REGSEL_2A_0, SRCREG1_2A_2, SRCREG2_2A_2;

  Counter #(.width(3), .max('h7)) counter_1 (
    .count(1'b1), .Q(counter_1_q), .clk(CLK), .clr(d_ff_1_q));  // open: load, D, carry
  D_Flip_Flop d_ff_1 (.clk(CLK), .D(Rewind), .Q(d_ff_1_q), .en(1'b1), .reset(d_ff_1_q));  // open: Qn, preset
  not not_1 (not_1_out, INSTRUCTION[4]);
  Decoder #(.select(3), .enable("false")) decoder_1 (
    .out0(T0), .out1(T1), .out2(T2), .out3(T3), .out4(T4), .out5(T5), .out6(T6), .out7(T7), .sel(counter_1_q));
  Decoder #(.select(2)) decoder_2 (
    .out0(SRCREG2_2A_2[0]), .out1(SRCREG2_2A_2[1]), .out2(SRCREG2_2A_2[2]), .out3(SRCREG2_2A_2[3]),
    .sel(INSTRUCTION[3:2]), .en(not_1_out));
  Decoder #(.select(2)) decoder_3 (
    .out0(decoder_3_out0), .out1(decoder_3_out1), .out2(SRCREG2_2B_2[1]), .out3(SRCREG2_2B_2[2]),
    .sel(INSTRUCTION[3:2]), .en(INSTRUCTION[4]));
  or or_1 (SRCREG2_2B_2[0], decoder_3_out0, decoder_3_out1);
  Decoder #(.select(5), .disabled(0), .enable("false")) decoder_4 (
    .out0(Opcode0), .out1(Opcode1), .out2(Opcode2), .out3(Opcode3), .out4(Opcode4), .out5(Opcode5),
    .out6(Opcode6), .out7(Opcode7), .out8(Opcode8), .out9(Opcode9), .out10(Opcode10), .out11(Opcode11),
    .out12(Opcode12), .out13(Opcode13), .out14(Opcode14), .out15(Opcode15), .out16(Opcode16),
    .out17(Opcode17), .out18(Opcode18), .sel(INSTRUCTION[15:11]));  // open: out19, out20, out21, out22, out23, out24, out25, out26, out27, out28, out29, out30, out31
  Decoder #(.select(2), .enable("false")) decoder_5 (
    .out0(REGSEL_2A_0[0]), .out1(REGSEL_2A_0[1]), .out2(REGSEL_2A_0[2]), .out3(REGSEL_2A_0[3]),
    .sel(INSTRUCTION[10:9]));
  not not_2 (not_2_out, INSTRUCTION[10]);
  not not_3 (not_3_out, INSTRUCTION[7]);
  Decoder #(.select(2)) decoder_6 (
    .out0(decoder_6_out0), .out1(decoder_6_out1), .out2(DESTREG_2B_2[1]), .out3(DESTREG_2B_2[2]),
    .sel(INSTRUCTION[9:8]), .en(INSTRUCTION[10]));
  or or_2 (DESTREG_2B_2[0], decoder_6_out0, decoder_6_out1);
  Decoder #(.select(2)) decoder_7 (
    .out0(SRCREG1_2A_2[0]), .out1(SRCREG1_2A_2[1]), .out2(SRCREG1_2A_2[2]), .out3(SRCREG1_2A_2[3]),
    .sel(INSTRUCTION[6:5]), .en(not_3_out));
  Decoder #(.select(2)) decoder_8 (
    .out0(decoder_8_out0), .out1(decoder_8_out1), .out2(SRCREG1_2B_2[1]), .out3(SRCREG1_2B_2[2]),
    .sel(INSTRUCTION[6:5]), .en(INSTRUCTION[7]));
  or or_3 (SRCREG1_2B_2[0], decoder_8_out0, decoder_8_out1);
  Decoder #(.select(2)) decoder_9 (
    .out0(DESTREG_2A_2[0]), .out1(DESTREG_2A_2[1]), .out2(DESTREG_2A_2[2]), .out3(DESTREG_2A_2[3]),
    .sel(INSTRUCTION[9:8]), .en(not_2_out));
  and and_1 (and_1_out, T4, Opcode1);
  and and_2 (and_2_out, T5, INSTRUCTION[8], Opcode0);
  and and_3 (and_3_out, T5, Opcode4);
  and and_4 (and_4_out, T5, Opcode18);
  and and_5 (and_5_out, T4, Opcode17);
  and and_6 (and_6_out, T4, Opcode3);
  assign L_H = T0 ? 1'b1 : 1'bz;  // Controlled_Buffer controlled_buffer_1
  assign L_H = T2 ? 1'b0 : 1'bz;  // Controlled_Buffer controlled_buffer_2
  or or_4 (or_4_out, T0, T2);
  or or_5 (or_5_out, and_5_out, and_1_out, and_6_out);
  or or_6 (or_6_out, T0, T2, and_2_out, and_3_out, and_4_out);
  or or_7 (EnableRam, or_5_out, or_6_out);
  or or_8 (Enable_2C, T0, T2);
  assign FunSel_2C = or_4_out ? 2'b11 : 2'bz;  // Controlled_Buffer controlled_buffer_3
  or or_9 (Opcode_2_7_8_11_12_13, Opcode2, Opcode7, Opcode8, Opcode11, Opcode12, Opcode13);
  or or_10 (Opcode_9_10_17, Opcode9, Opcode10, Opcode17);
  or or_11 (Opcode_11_12_13, Opcode11, Opcode12, Opcode13);
  or or_12 (Opcode_2_7, Opcode2, Opcode7);
  or or_13 (Opcode_2_7_8, Opcode2, Opcode7, Opcode8);
  or or_14 (Opcode_9_10, Opcode9, Opcode10);
  assign Read = or_5_out ? 1'b0 : 1'bz;  // Controlled_Buffer controlled_buffer_4
  assign Read = or_6_out ? 1'b1 : 1'bz;  // Controlled_Buffer controlled_buffer_5
  not not_4 (Load, Read);
  not not_5 (not_5_out, INSTRUCTION[7]);
  not not_6 (not_6_out, INSTRUCTION[4]);
  not not_7 (not_7_out, INSTRUCTION[7]);
  not not_8 (not_8_out, INSTRUCTION[7]);
  not not_9 (not_9_out, INSTRUCTION[4]);
  not not_10 (not_10_out, INSTRUCTION[8]);
  xor xor_1 (xor_1_out, INSTRUCTION[7], INSTRUCTION[10]);
  not not_11 (not_11_out, INSTRUCTION[10]);
  and and_7 (and_7_out, not_5_out, not_6_out);
  and and_8 (and_8_out, not_7_out, INSTRUCTION[4]);
  and and_9 (and_9_out, not_8_out, not_9_out);
  or or_15 (Opcode11_Opcode12_Opcode13, Opcode11, Opcode12, Opcode13);
  not not_12 (not_12_out, INSTRUCTION[10]);
  not not_13 (not_13_out, INSTRUCTION[10]);
  not not_14 (not_14_out, INSTRUCTION[10]);
  not not_15 (not_15_out, INSTRUCTION[10]);
  not not_16 (not_16_out, INSTRUCTION[10]);
  not not_17 (not_17_out, INSTRUCTION[10]);
  or or_16 (Opcode7_Opcode8, Opcode8, Opcode7);
  and and_10 (and_10_out, not_11_out, T5, Opcode11_Opcode12_Opcode13);
  and and_11 (and_11_out, Opcode0, INSTRUCTION[8], T5);
  and and_12 (and_12_out, T5, Opcode4);
  and and_13 (and_13_out, Opcode0, not_10_out, T4);
  and and_14 (and_14_out, not_15_out, T5, and_8_out, Opcode6);
  and and_15 (and_15_out, not_16_out, T4, and_9_out, Opcode5);
  and and_16 (and_16_out, not_17_out, T4, Opcode7_Opcode8);
  not not_18 (not_18_out, INSTRUCTION[10]);
  not not_19 (not_19_out, INSTRUCTION[10]);
  and and_17 (and_17_out, not_12_out, T4, Opcode2);
  and and_18 (and_18_out, not_13_out, T5, xor_1_out, Opcode5_Opcode9_Opcode10);
  and and_19 (and_19_out, not_14_out, T4, and_7_out, Opcode6_Opcode9_Opcode10);
  and and_20 (and_20_out, not_18_out, Opcode7, T5);
  and and_21 (and_21_out, not_19_out, Opcode8, T5);
  or or_17 (or_17_out, and_10_out, and_11_out, and_12_out, and_13_out, and_17_out, and_18_out, and_19_out, and_14_out, and_15_out, and_16_out);
  assign FunSel2A = and_20_out ? 2'b11 : 2'bz;  // Controlled_Buffer controlled_buffer_6
  assign FunSel2A = and_21_out ? 2'b10 : 2'bz;  // Controlled_Buffer controlled_buffer_7
  or or_18 (Opcode5_Opcode9_Opcode10, Opcode5, Opcode9, Opcode10);
  or or_19 (Opcode6_Opcode9_Opcode10, Opcode6, Opcode9, Opcode10);
  assign FunSel2A = or_17_out ? 2'b01 : 2'bz;  // Controlled_Buffer controlled_buffer_8
  or or_20 (or_20_out, T1, T3);
  not not_20 (not_20_out, INSTRUCTION[4]);
  xor xor_2 (xor_2_out, INSTRUCTION[7], INSTRUCTION[4]);
  not not_21 (not_21_out, Z);
  not not_22 (not_22_out, INSTRUCTION[4]);
  not not_23 (not_23_out, INSTRUCTION[7]);
  not not_24 (not_24_out, INSTRUCTION[7]);
  or or_21 (or_21_out, Opcode18, Opcode4);
  and and_22 (and_22_out, T5, Opcode17);
  or or_22 (Opcode2_Opcode7_Opcode8, Opcode2, Opcode7, Opcode8);
  and and_23 (and_23_out, T4, INSTRUCTION[10], Opcode5, not_20_out);
  and and_24 (and_24_out, T4, INSTRUCTION[10], Opcode2_Opcode7_Opcode8);
  and and_25 (and_25_out, T4, INSTRUCTION[10], xor_2_out, Opcode_9_10);
  and and_26 (and_26_out, T4, Opcode14);
  and and_27 (and_27_out, T4, Opcode15, Z);
  and and_28 (and_28_out, T4, Opcode16, not_21_out);
  and and_29 (and_29_out, T6, Opcode17);
  and and_30 (and_30_out, T5, Opcode18);
  and and_31 (and_31_out, T4, INSTRUCTION[10], Opcode6_Opcode9_Opcode10, not_22_out, not_23_out);
  and and_32 (and_32_out, T4, INSTRUCTION[10], Opcode6, not_24_out);
  and and_33 (and_33_out, T4, or_21_out);
  and and_34 (and_34_out, T5, INSTRUCTION[10], Opcode8);
  and and_35 (and_35_out, T4, Opcode3);
  and and_36 (and_36_out, T5, INSTRUCTION[10], Opcode7);
  and and_37 (and_37_out, T5, INSTRUCTION[10], Opcode_11_12_13);
  or or_23 (or_23_out, and_33_out, or_20_out, and_34_out);
  or or_24 (or_24_out, and_35_out, and_22_out, and_36_out);
  or or_25 (or_25_out, and_23_out, and_24_out, and_25_out, and_26_out, and_27_out, and_28_out, and_29_out, and_30_out, and_31_out, and_32_out, and_37_out);
  assign FunSel2B = or_23_out ? 2'b10 : 2'bz;  // Controlled_Buffer controlled_buffer_9
  assign FunSel2B = or_24_out ? 2'b11 : 2'bz;  // Controlled_Buffer controlled_buffer_10
  assign FunSel2B = or_25_out ? 2'b01 : 2'bz;  // Controlled_Buffer controlled_buffer_11
  or or_26 (or_26_out, Opcode8, Opcode7);
  not not_25 (not_25_out, INSTRUCTION[4]);
  not not_26 (not_26_out, INSTRUCTION[10]);
  not not_27 (not_27_out, INSTRUCTION[10]);
  and and_38 (and_38_out, T6, or_26_out);
  not not_28 (not_28_out, INSTRUCTION[4]);
  not not_29 (not_29_out, INSTRUCTION[10]);
  not not_30 (not_30_out, INSTRUCTION[7]);
  not not_31 (not_31_out, INSTRUCTION[10]);
  not not_32 (not_32_out, INSTRUCTION[7]);
  not not_33 (not_33_out, INSTRUCTION[10]);
  or or_27 (or_27_out, Opcode17, Opcode1);
  and and_39 (and_39_out, INSTRUCTION[7], INSTRUCTION[10]);
  or or_28 (or_28_out, Opcode2, Opcode7, Opcode8);
  not not_34 (not_34_out, INSTRUCTION[7]);
  and and_40 (and_40_out, T4, and_39_out, or_28_out);
  or or_29 (or_29_out, Opcode2, Opcode7, Opcode8);
  not not_35 (not_35_out, INSTRUCTION[4]);
  not not_36 (not_36_out, INSTRUCTION[7]);
  not not_37 (not_37_out, INSTRUCTION[4]);
  not not_38 (not_38_out, INSTRUCTION[7]);
  and and_41 (and_41_out, T4, not_27_out, INSTRUCTION[10], INSTRUCTION[7], Opcode10);
  not not_39 (not_39_out, INSTRUCTION[10]);
  not not_40 (not_40_out, INSTRUCTION[4]);
  not not_41 (not_41_out, INSTRUCTION[7]);
  not not_42 (not_42_out, INSTRUCTION[7]);
  not not_43 (not_43_out, INSTRUCTION[4]);
  not not_44 (not_44_out, INSTRUCTION[10]);
  not not_45 (not_45_out, INSTRUCTION[4]);
  not not_46 (not_46_out, INSTRUCTION[7]);
  and and_42 (and_42_out, T4, or_27_out);
  and and_43 (and_43_out, Opcode3, T4);
  and and_44 (and_44_out, T4, not_34_out, or_29_out);
  and and_45 (and_45_out, T4, not_35_out, not_36_out, Opcode9);
  and and_46 (and_46_out, T5, INSTRUCTION[7], not_28_out, not_29_out, Opcode9);
  and and_47 (and_47_out, T5, not_28_out, not_29_out, INSTRUCTION[4], Opcode9);
  and and_48 (and_48_out, T4, INSTRUCTION[4], not_30_out, INSTRUCTION[4], Opcode9);
  and and_49 (and_49_out, T4, not_31_out, INSTRUCTION[10], INSTRUCTION[7], Opcode9);
  and and_50 (and_50_out, T4, not_37_out, not_38_out, Opcode10);
  and and_51 (and_51_out, T5, INSTRUCTION[7], not_25_out, not_26_out, Opcode10);
  and and_52 (and_52_out, T5, not_25_out, not_26_out, INSTRUCTION[4], Opcode10);
  and and_53 (and_53_out, T4, INSTRUCTION[4], not_32_out, INSTRUCTION[4], Opcode10);
  and and_54 (and_54_out, T4, not_39_out, not_40_out, Opcode5, not_41_out);
  and and_55 (and_55_out, T5, not_33_out, INSTRUCTION[4], Opcode5, not_42_out);
  and and_56 (and_56_out, T5, INSTRUCTION[7], not_43_out, Opcode5, not_44_out);
  and and_57 (and_57_out, T4, INSTRUCTION[10], not_45_out, Opcode5);
  not not_47 (not_47_out, INSTRUCTION[7]);
  not not_48 (not_48_out, INSTRUCTION[10]);
  not not_49 (not_49_out, INSTRUCTION[7]);
  or or_30 (or_30_out, and_42_out, and_38_out, and_40_out);
  or or_31 (or_31_out, and_43_out, and_44_out);
  and and_58 (and_58_out, T4, INSTRUCTION[10], INSTRUCTION[4], Opcode5, not_47_out);
  and and_59 (and_59_out, INSTRUCTION[10], not_46_out, T4, Opcode6);
  and and_60 (and_60_out, not_48_out, not_49_out, T5, Opcode6);
  or or_32 (or_32_out, and_45_out, and_46_out, and_47_out, and_48_out, and_49_out);
  or or_33 (or_33_out, and_50_out, and_51_out, and_52_out, and_53_out, and_41_out);
  or or_34 (or_34_out, and_54_out, and_55_out, and_56_out, and_57_out, and_58_out);
  assign FunSel_ALU = or_30_out ? 4'b0000 : 4'bz;  // Controlled_Buffer controlled_buffer_12
  assign FunSel_ALU = or_31_out ? 4'b0001 : 4'bz;  // Controlled_Buffer controlled_buffer_13
  assign FunSel_ALU = or_32_out ? 4'b0111 : 4'bz;  // Controlled_Buffer controlled_buffer_14
  assign FunSel_ALU = or_33_out ? 4'b1000 : 4'bz;  // Controlled_Buffer controlled_buffer_15
  and and_61 (and_61_out, T4, Opcode12);
  assign FunSel_ALU = and_61_out ? 4'b1010 : 4'bz;  // Controlled_Buffer controlled_buffer_16
  and and_62 (and_62_out, T4, Opcode13);
  assign FunSel_ALU = and_62_out ? 4'b1011 : 4'bz;  // Controlled_Buffer controlled_buffer_17
  and and_63 (and_63_out, T4, Opcode11);
  assign FunSel_ALU = and_63_out ? 4'b0010 : 4'bz;  // Controlled_Buffer controlled_buffer_18
  assign FunSel_ALU = or_34_out ? 4'b0100 : 4'bz;  // Controlled_Buffer controlled_buffer_19
  or or_35 (or_35_out, and_59_out, and_60_out);
  assign FunSel_ALU = or_35_out ? 4'b0110 : 4'bz;  // Controlled_Buffer controlled_buffer_20
  not not_50 (not_50_out, INSTRUCTION[7]);
  not not_51 (not_51_out, INSTRUCTION[4]);
  not not_52 (not_52_out, INSTRUCTION[10]);
  not not_53 (not_53_out, INSTRUCTION[10]);
  not not_54 (not_54_out, INSTRUCTION[7]);
  or or_36 (or_36_out, Opcode9, Opcode10);
  or or_37 (or_37_out, Opcode11, Opcode12, Opcode13);
  and and_64 (and_64_out, INSTRUCTION[8], Opcode0, T5);
  and and_65 (and_65_out, Opcode1, T4);
  not not_55 (not_55_out, INSTRUCTION[4]);
  not not_56 (not_56_out, INSTRUCTION[7]);
  not not_57 (not_57_out, INSTRUCTION[7]);
  and and_66 (and_66_out, not_50_out, not_51_out, Opcode5, T4);
  and and_67 (and_67_out, not_52_out, Opcode7, Opcode7, T6);
  and and_68 (and_68_out, not_53_out, not_54_out, Opcode8, T6);
  and and_69 (and_69_out, not_55_out, not_56_out, or_36_out, T4);
  and and_70 (and_70_out, not_57_out, or_37_out, T4);
  or or_38 (or_38_out, and_64_out, and_65_out);
  assign OUTASEL = or_38_out ? INSTRUCTION[10:9] : 2'bz;  // Controlled_Buffer controlled_buffer_21
  or or_39 (or_39_out, and_66_out, and_67_out, and_68_out);
  assign OUTASEL = or_39_out ? INSTRUCTION[6:5] : 2'bz;  // Controlled_Buffer controlled_buffer_22
  or or_40 (or_40_out, and_69_out, and_70_out);
  assign OUTASEL = or_40_out ? SRCREG1_2A_2[1:0] : 2'bz;  // Controlled_Buffer controlled_buffer_23
  not not_58 (not_58_out, INSTRUCTION[4]);
  not not_59 (not_59_out, INSTRUCTION[10]);
  not not_60 (not_60_out, INSTRUCTION[7]);
  not not_61 (not_61_out, INSTRUCTION[10]);
  and and_71 (and_71_out, T5, not_58_out, not_59_out, IR17, Opcode5);
  and and_72 (and_72_out, T4, not_60_out, not_61_out, INSTRUCTION[4], Opcode5);
  not not_62 (not_62_out, INSTRUCTION[7]);
  not not_63 (not_63_out, INSTRUCTION[7]);
  not not_64 (not_64_out, INSTRUCTION[10]);
  not not_65 (not_65_out, INSTRUCTION[4]);
  not not_66 (not_66_out, INSTRUCTION[7]);
  or or_41 (or_41_out, Opcode7, Opcode8);
  not not_67 (not_67_out, INSTRUCTION[7]);
  not not_68 (not_68_out, INSTRUCTION[7]);
  not not_69 (not_69_out, INSTRUCTION[7]);
  or or_42 (or_42_out, Opcode9, Opcode10);
  not not_70 (not_70_out, INSTRUCTION[4]);
  or or_43 (or_43_out, Opcode9, Opcode10);
  not not_71 (not_71_out, INSTRUCTION[4]);
  or or_44 (or_44_out, Opcode9, Opcode10);
  and and_73 (and_73_out, T4, not_65_out, Opcode5);
  and and_74 (and_74_out, T4, not_67_out, Opcode6);
  and and_75 (and_75_out, not_68_out, Opcode2, T4);
  not not_72 (not_72_out, INSTRUCTION[10]);
  not not_73 (not_73_out, INSTRUCTION[4]);
  not not_74 (not_74_out, INSTRUCTION[7]);
  and and_76 (and_76_out, T4, not_70_out, not_62_out, or_43_out);
  and and_77 (and_77_out, T4, INSTRUCTION[7], not_71_out, or_44_out);
  and and_78 (and_78_out, T4, not_63_out, Opcode5);
  and and_79 (and_79_out, T4, not_66_out, or_41_out);
  and and_80 (and_80_out, T5, not_72_out, INSTRUCTION[7], Opcode5);
  and and_81 (and_81_out, T4, not_74_out, Opcode6);
  and and_82 (and_82_out, T4, not_69_out, or_42_out);
  or or_45 (or_45_out, and_78_out, and_72_out, and_73_out);
  assign OUTBSEL = or_45_out ? INSTRUCTION[3:2] : 2'bz;  // Controlled_Buffer controlled_buffer_24
  or or_46 (or_46_out, and_79_out, and_71_out, and_74_out, and_75_out);
  assign OUTBSEL = or_46_out ? INSTRUCTION[6:5] : 2'bz;  // Controlled_Buffer controlled_buffer_25
  assign OUTBSEL = and_80_out ? INSTRUCTION[10:9] : 2'bz;  // Controlled_Buffer controlled_buffer_26
  or or_47 (or_47_out, and_76_out, and_77_out);
  assign OUTBSEL = or_47_out ? SRCREG2_2A_2[1:0] : 2'bz;  // Controlled_Buffer controlled_buffer_27
  or or_48 (or_48_out, and_81_out, and_82_out);
  assign OUTBSEL = or_48_out ? SRCREG1_2A_2[1:0] : 2'bz;  // Controlled_Buffer controlled_buffer_28
  not not_75 (not_75_out, INSTRUCTION[7]);
  not not_76 (not_76_out, INSTRUCTION[7]);
  not not_77 (not_77_out, INSTRUCTION[10]);
  not not_78 (not_78_out, INSTRUCTION[7]);
  not not_79 (not_79_out, INSTRUCTION[10]);
  not not_80 (not_80_out, INSTRUCTION[4]);
  not not_81 (not_81_out, INSTRUCTION[4]);
  not not_82 (not_82_out, INSTRUCTION[4]);
  or or_49 (or_49_out, Opcode8, Opcode7);
  or or_50 (or_50_out, Opcode9, Opcode10);
  or or_51 (or_51_out, Opcode9, Opcode10);
  or or_52 (or_52_out, Opcode11, Opcode12, Opcode13);
  and and_83 (and_83_out, T4, INSTRUCTION[4], not_75_out, INSTRUCTION[10], Opcode6);
  and and_84 (and_84_out, T4, INSTRUCTION[7], or_49_out);
  and and_85 (and_85_out, T4, INSTRUCTION[4], not_76_out, or_50_out);
  and and_86 (and_86_out, T5, INSTRUCTION[4], INSTRUCTION[7], not_77_out, Opcode5);
  and and_87 (and_87_out, T6, INSTRUCTION[10], Opcode7);
  and and_88 (and_88_out, T6, INSTRUCTION[7], Opcode8);
  and and_89 (and_89_out, T6, INSTRUCTION[10], not_78_out, Opcode8);
  and and_90 (and_90_out, T4, INSTRUCTION[7], Opcode2);
  and and_91 (and_91_out, T4, INSTRUCTION[4], not_79_out, Opcode5);
  and and_92 (and_92_out, T4, not_80_out, INSTRUCTION[7], Opcode5);
  and and_93 (and_93_out, T4, not_81_out, INSTRUCTION[7], INSTRUCTION[10], Opcode6);
  and and_94 (and_94_out, T4, not_82_out, INSTRUCTION[7], or_51_out);
  and and_95 (and_95_out, T4, INSTRUCTION[7], or_52_out);
  and and_96 (and_96_out, T4, Opcode17);
  or or_53 (or_53_out, and_87_out, and_88_out, and_89_out);
  or or_54 (or_54_out, and_83_out, and_84_out, and_85_out, and_86_out);
  assign OUTCSEL = or_53_out ? DESTREG_2B_2[1:0] : 2'bz;  // Controlled_Buffer controlled_buffer_29
  or or_55 (or_55_out, and_96_out, T1);
  or or_56 (or_56_out, and_90_out, and_91_out, and_92_out, and_93_out, and_94_out, and_95_out);
  assign OUTCSEL = or_54_out ? SRCREG1_2B_2[2:1] : 2'bz;  // Controlled_Buffer controlled_buffer_30
  assign OUTCSEL = or_55_out ? 2'b00 : 2'bz;  // Controlled_Buffer controlled_buffer_31
  assign OUTCSEL = or_56_out ? SRCREG1_2B_2[1:0] : 2'bz;  // Controlled_Buffer controlled_buffer_32
  or or_57 (or_57_out, Opcode7, Opcode8);
  or or_58 (or_58_out, Opcode_9_10, Opcode6);
  or or_59 (or_59_out, Opcode5, Opcode6);
  or or_60 (or_60_out, T4, T5, T6);
  not not_83 (not_83_out, INSTRUCTION[4]);
  or or_61 (or_61_out, Opcode5, Opcode6);
  not not_84 (not_84_out, INSTRUCTION[4]);
  not not_85 (not_85_out, INSTRUCTION[7]);
  not not_86 (not_86_out, INSTRUCTION[7]);
  not not_87 (not_87_out, INSTRUCTION[10]);
  not not_88 (not_88_out, INSTRUCTION[4]);
  not not_89 (not_89_out, INSTRUCTION[7]);
  not not_90 (not_90_out, INSTRUCTION[4]);
  not not_91 (not_91_out, INSTRUCTION[10]);
  not not_92 (not_92_out, INSTRUCTION[10]);
  not not_93 (not_93_out, INSTRUCTION[7]);
  not not_94 (not_94_out, INSTRUCTION[10]);
  not not_95 (not_95_out, INSTRUCTION[10]);
  not not_96 (not_96_out, INSTRUCTION[7]);
  not not_97 (not_97_out, INSTRUCTION[10]);
  not not_98 (not_98_out, INSTRUCTION[4]);
  not not_99 (not_99_out, INSTRUCTION[10]);
  not not_100 (not_100_out, INSTRUCTION[7]);
  not not_101 (not_101_out, INSTRUCTION[10]);
  not not_102 (not_102_out, INSTRUCTION[7]);
  not not_103 (not_103_out, INSTRUCTION[7]);
  not not_104 (not_104_out, INSTRUCTION[10]);
  not not_105 (not_105_out, INSTRUCTION[7]);
  not not_106 (not_106_out, INSTRUCTION[10]);
  and and_97 (and_97_out, T4, not_84_out, not_85_out, not_107_out, or_58_out);
  not not_107 (not_107_out, INSTRUCTION[10]);
  and and_98 (and_98_out, T5, INSTRUCTION[4], not_86_out, not_87_out, Opcode_9_10);
  and and_99 (and_99_out, T5, not_88_out, not_89_out, INSTRUCTION[10], Opcode9);
  and and_100 (and_100_out, T5, not_90_out, INSTRUCTION[7], not_91_out, Opcode10);
  and and_101 (and_101_out, T5, not_92_out, Opcode_11_12_13);
  and and_102 (and_102_out, T5, not_93_out, not_94_out, Opcode8);
  not not_108 (not_108_out, INSTRUCTION[8]);
  and and_103 (and_103_out, INSTRUCTION[7], Opcode_2_7_8_11_12_13, T4);
  and and_104 (and_104_out, T4, Opcode_9_10_17);
  and and_105 (and_105_out, not_95_out, not_96_out, INSTRUCTION[4], or_59_out, T4);
  and and_106 (and_106_out, not_97_out, INSTRUCTION[7], not_98_out, Opcode5, T4);
  and and_107 (and_107_out, not_99_out, INSTRUCTION[7], INSTRUCTION[4], Opcode5, or_60_out);
  and and_108 (and_108_out, INSTRUCTION[10], INSTRUCTION[7], not_83_out, Opcode5, T4);
  and and_109 (and_109_out, T6, or_57_out, not_101_out, not_102_out);
  and and_110 (and_110_out, T6, or_57_out, INSTRUCTION[10], INSTRUCTION[7]);
  and and_111 (and_111_out, T4, not_103_out, not_104_out, Opcode_2_7);
  and and_112 (and_112_out, T4, not_105_out, not_106_out, Opcode5);
  and and_113 (and_113_out, T4, not_108_out, Opcode0);
  and and_114 (and_114_out, INSTRUCTION[10], not_100_out, INSTRUCTION[4], T4, or_61_out);
  and and_115 (and_115_out, T5, INSTRUCTION[8], Opcode0);
  and and_116 (and_116_out, T5, Opcode4);
  or or_62 (or_62_out, and_115_out, and_116_out);
  or or_63 (or_63_out, and_103_out, and_104_out, and_105_out, and_106_out, and_107_out, and_108_out, and_114_out, and_109_out, and_110_out);
  or or_64 (or_64_out, and_111_out, and_112_out, and_97_out, and_98_out, and_99_out, and_100_out, and_101_out, and_102_out);
  buf or_65 (or_65_out, and_113_out);  // OR_Gate
  assign MuxASel = or_65_out ? 2'b00 : 2'bz;  // Controlled_Buffer controlled_buffer_33
  assign MuxASel = or_62_out ? 2'b01 : 2'bz;  // Controlled_Buffer controlled_buffer_34
  assign MuxASel = or_63_out ? 2'b10 : 2'bz;  // Controlled_Buffer controlled_buffer_35
  assign MuxASel = or_64_out ? 2'b11 : 2'bz;  // Controlled_Buffer controlled_buffer_36
  or or_66 (MuxASelEnable, or_64_out, or_62_out, or_65_out, or_63_out);
  not not_109 (not_109_out, INSTRUCTION[4]);
  not not_110 (not_110_out, INSTRUCTION[7]);
  not not_111 (not_111_out, INSTRUCTION[7]);
  not not_112 (not_112_out, INSTRUCTION[4]);
  not not_113 (not_113_out, INSTRUCTION[4]);
  not not_114 (not_114_out, INSTRUCTION[7]);
  not not_115 (not_115_out, Z);
  not not_116 (not_116_out, INSTRUCTION[7]);
  not not_117 (not_117_out, INSTRUCTION[10]);
  and and_117 (and_117_out, T4, INSTRUCTION[10], not_114_out, Opcode6);
  and and_118 (and_118_out, T4, not_115_out, Opcode16);
  and and_119 (and_119_out, T4, Opcode15);
  and and_120 (and_120_out, T4, Opcode14);
  and and_121 (and_121_out, T7, Opcode17);
  and and_122 (and_122_out, T5, Opcode18);
  and and_123 (and_123_out, T4, INSTRUCTION[10], Opcode_2_7_8);
  and and_124 (and_124_out, T4, not_116_out, not_117_out, Opcode2);
  and and_125 (and_125_out, T4, not_109_out, not_110_out, INSTRUCTION[10], Opcode_9_10);
  and and_126 (and_126_out, T4, INSTRUCTION[4], not_111_out, INSTRUCTION[10], Opcode_9_10);
  and and_127 (and_127_out, T4, not_112_out, INSTRUCTION[7], INSTRUCTION[10], Opcode_9_10);
  and and_128 (and_128_out, T5, INSTRUCTION[10], Opcode_11_12_13);
  and and_129 (and_129_out, T4, INSTRUCTION[10], not_113_out, Opcode5);
  or or_67 (or_67_out, and_118_out, and_119_out, and_120_out, and_121_out);
  or or_68 (or_68_out, and_129_out, and_123_out, and_124_out, and_125_out, and_126_out, and_127_out, and_128_out, and_117_out);
  or or_69 (MuxBSelEnable, or_67_out, and_122_out, or_68_out);
  assign MuxBSel = or_67_out ? 2'b01 : 2'bz;  // Controlled_Buffer controlled_buffer_37
  assign MuxBSel = and_122_out ? 2'b10 : 2'bz;  // Controlled_Buffer controlled_buffer_38
  assign MuxBSel = or_68_out ? 2'b11 : 2'bz;  // Controlled_Buffer controlled_buffer_39
  not not_118 (not_118_out, INSTRUCTION[7]);
  not not_119 (not_119_out, INSTRUCTION[4]);
  not not_120 (not_120_out, INSTRUCTION[7]);
  not not_121 (not_121_out, INSTRUCTION[10]);
  not not_122 (not_122_out, INSTRUCTION[4]);
  not not_123 (not_123_out, INSTRUCTION[10]);
  or or_70 (or_70_out, Opcode5, Opcode6);
  not not_124 (not_124_out, INSTRUCTION[10]);
  not not_125 (not_125_out, INSTRUCTION[7]);
  not not_126 (not_126_out, INSTRUCTION[7]);
  not not_127 (not_127_out, INSTRUCTION[4]);
  not not_128 (not_128_out, INSTRUCTION[4]);
  not not_129 (not_129_out, INSTRUCTION[7]);
  or or_71 (or_71_out, Opcode5, Opcode6);
  or or_72 (or_72_out, Opcode7, Opcode8);
  and and_130 (and_130_out, T4, Opcode_2_7_8, INSTRUCTION[7], INSTRUCTION[10]);
  and and_131 (and_131_out, T4, Opcode_9_10, INSTRUCTION[4], not_118_out);
  and and_132 (and_132_out, T4, Opcode_9_10, INSTRUCTION[7], not_119_out);
  and and_133 (and_133_out, T4, Opcode17);
  and and_134 (and_134_out, T4, INSTRUCTION[4], not_120_out, not_121_out, Opcode5);
  and and_135 (and_135_out, T4, INSTRUCTION[7], not_122_out, not_123_out, or_70_out);
  and and_136 (and_136_out, T5, INSTRUCTION[4], INSTRUCTION[7], not_124_out, Opcode5);
  and and_137 (and_137_out, T4, INSTRUCTION[4], not_125_out, INSTRUCTION[10], or_73_out);
  or or_73 (or_73_out, Opcode5, Opcode6);
  or or_74 (or_74_out, Opcode7, Opcode8);
  and and_138 (and_138_out, T4, Opcode1);
  and and_139 (and_139_out, T4, Opcode_9_10, not_126_out, not_127_out);
  and and_140 (and_140_out, T4, Opcode_11_12_13);
  and and_141 (and_141_out, T4, not_128_out, not_129_out, or_71_out);
  not not_130 (not_130_out, INSTRUCTION[10]);
  and and_142 (and_142_out, T6, INSTRUCTION[10], or_74_out);
  or or_75 (or_75_out, and_138_out, and_139_out, and_140_out, and_141_out, and_143_out);
  and and_143 (and_143_out, T6, not_130_out, or_72_out);
  or or_76 (or_76_out, and_130_out, and_131_out, and_132_out, and_133_out, and_134_out, and_135_out, and_136_out, and_137_out, and_142_out);
  or or_77 (MuxCSelEnable, or_76_out, or_75_out);
  assign MuxCSel = or_76_out ? 1'b0 : 1'bz;  // Controlled_Buffer controlled_buffer_40
  assign MuxCSel = or_75_out ? 1'b1 : 1'bz;  // Controlled_Buffer controlled_buffer_41
  or or_78 (or_78_out, Opcode10, Opcode5, Opcode6, Opcode9);
  or or_79 (or_79_out, Opcode10, Opcode5, Opcode6, Opcode9);
  or or_80 (or_80_out, Opcode12, Opcode1, Opcode4, Opcode13, Opcode18);
  or or_81 (or_81_out, Opcode14, Opcode2, Opcode3, Opcode15, Opcode16);
  not not_131 (not_131_out, INSTRUCTION[4]);
  not not_132 (not_132_out, INSTRUCTION[7]);
  or or_82 (or_82_out, Opcode10, Opcode6, Opcode9);
  or or_83 (or_83_out, Opcode7, Opcode17, Opcode8);
  not not_133 (not_133_out, INSTRUCTION[10]);
  xor xor_3 (xor_3_out, INSTRUCTION[4], INSTRUCTION[7]);
  xor xor_4 (xor_4_out, INSTRUCTION[4], INSTRUCTION[7]);
  not not_134 (not_134_out, INSTRUCTION[8]);
  and and_144 (and_144_out, not_133_out, xor_3_out, or_78_out, T5);
  and and_145 (and_145_out, or_80_out, T5);
  and and_146 (and_146_out, or_81_out, T4);
  and and_147 (and_147_out, or_83_out, T6);
  and and_148 (and_148_out, Opcode0, INSTRUCTION[8], T5);
  and and_149 (and_149_out, Opcode0, not_134_out, T4);
  and and_150 (and_150_out, not_131_out, not_132_out, or_82_out, T4);
  // AND_Gate and_151 has open pins: in0=INSTRUCTION[10], in1=xor_4_out, in2=or_79_out, in4=T4, out=open
  or or_84 (Rewind, and_150_out, and_144_out, and_145_out, and_149_out, and_146_out, and_147_out, and_148_out);
  and and_152 (and_152_out, Opcode0, INSTRUCTION[8], T4);
  and and_153 (and_153_out, Opcode1, T4);
  and and_154 (and_154_out, Opcode4, T5);
  and and_155 (and_155_out, Opcode17, T4);
  and and_156 (and_156_out, Opcode18, T5);
  not not_135 (not_135_out, Z);
  and and_157 (and_157_out, Opcode16, T4, not_135_out);
  or or_85 (or_85_out, and_152_out, and_153_out);
  or or_86 (or_86_out, and_154_out, and_155_out, and_156_out);
  or or_87 (or_87_out, T0, T2, and_157_out);
  assign OutDSel = or_87_out ? 2'b00 : 2'bz;  // Controlled_Buffer controlled_buffer_42
  assign OutDSel = or_85_out ? 2'b01 : 2'bz;  // Controlled_Buffer controlled_buffer_43
  assign OutDSel = or_86_out ? 2'b10 : 2'bz;  // Controlled_Buffer controlled_buffer_44
  not not_136 (not_136_out, INSTRUCTION[10]);
  not not_137 (not_137_out, INSTRUCTION[10]);
  not not_138 (not_138_out, INSTRUCTION[7]);
  not not_139 (not_139_out, INSTRUCTION[10]);
  not not_140 (not_140_out, INSTRUCTION[7]);
  not not_141 (not_141_out, INSTRUCTION[10]);
  not not_142 (not_142_out, INSTRUCTION[10]);
  not not_143 (not_143_out, INSTRUCTION[7]);
  not not_144 (not_144_out, INSTRUCTION[10]);
  not not_145 (not_145_out, INSTRUCTION[7]);
  not not_146 (not_146_out, INSTRUCTION[10]);
  not not_147 (not_147_out, INSTRUCTION[7]);
  not not_148 (not_148_out, INSTRUCTION[4]);
  not not_149 (not_149_out, INSTRUCTION[10]);
  not not_150 (not_150_out, INSTRUCTION[7]);
  not not_151 (not_151_out, INSTRUCTION[10]);
  not not_152 (not_152_out, INSTRUCTION[4]);
  not not_153 (not_153_out, INSTRUCTION[10]);
  not not_154 (not_154_out, INSTRUCTION[7]);
  not not_155 (not_155_out, INSTRUCTION[4]);
  not not_156 (not_156_out, INSTRUCTION[10]);
  not not_157 (not_157_out, INSTRUCTION[7]);
  not not_158 (not_158_out, INSTRUCTION[10]);
  not not_159 (not_159_out, INSTRUCTION[4]);
  not not_160 (not_160_out, INSTRUCTION[10]);
  not not_161 (not_161_out, INSTRUCTION[7]);
  not not_162 (not_162_out, INSTRUCTION[10]);
  not not_163 (not_163_out, INSTRUCTION[10]);
  not not_164 (not_164_out, INSTRUCTION[7]);
  not not_165 (not_165_out, INSTRUCTION[10]);
  not not_166 (not_166_out, INSTRUCTION[10]);
  not not_167 (not_167_out, INSTRUCTION[7]);
  not not_168 (not_168_out, INSTRUCTION[10]);
  not not_169 (not_169_out, INSTRUCTION[10]);
  not not_170 (not_170_out, INSTRUCTION[8]);
  and and_158 (and_158_out, Opcode1, T4);
  and and_159 (and_159_out, Opcode4, T5);
  not not_171 (not_171_out, INSTRUCTION[10]);
  not not_172 (not_172_out, INSTRUCTION[10]);
  not not_173 (not_173_out, INSTRUCTION[7]);
  and and_160 (and_160_out, not_158_out, Opcode10, not_159_out, INSTRUCTION[7], T5);
  and and_161 (and_161_out, not_160_out, Opcode11, not_161_out, T5);
  and and_162 (and_162_out, not_162_out, Opcode11, INSTRUCTION[7], T5);
  and and_163 (and_163_out, not_163_out, Opcode12, not_164_out, T5);
  and and_164 (and_164_out, not_165_out, Opcode12, INSTRUCTION[7], T5);
  and and_165 (and_165_out, not_166_out, Opcode13, not_167_out, T5);
  and and_166 (and_166_out, not_168_out, Opcode13, INSTRUCTION[7], T5);
  and and_167 (and_167_out, not_169_out, Opcode5, T4);
  and and_168 (and_168_out, not_170_out, Opcode0, T4);
  and and_169 (and_169_out, INSTRUCTION[8], Opcode0, T5);
  and and_170 (and_170_out, not_171_out, Opcode2, INSTRUCTION[7], T4);
  and and_171 (and_171_out, not_172_out, Opcode2, not_173_out, T4);
  and and_172 (and_172_out, not_136_out, Opcode7, INSTRUCTION[7], T4);
  and and_173 (and_173_out, not_137_out, Opcode7, not_138_out, T4);
  and and_174 (and_174_out, not_139_out, Opcode7, not_140_out, T5);
  and and_175 (and_175_out, not_141_out, Opcode8, INSTRUCTION[7], T4);
  and and_176 (and_176_out, not_142_out, Opcode8, not_143_out, T4);
  and and_177 (and_177_out, not_144_out, Opcode8, not_145_out, T5);
  and and_178 (and_178_out, not_146_out, Opcode9, not_148_out, not_147_out, T4);
  and and_179 (and_179_out, not_149_out, Opcode9, INSTRUCTION[4], not_150_out, T5);
  and and_180 (and_180_out, not_151_out, Opcode9, not_152_out, INSTRUCTION[7], T5);
  and and_181 (and_181_out, not_153_out, Opcode10, not_155_out, not_154_out, T4);
  and and_182 (and_182_out, not_156_out, Opcode10, INSTRUCTION[4], not_157_out, T5);
  or or_88 (or_88_out, and_169_out, and_158_out, and_159_out, and_168_out);
  or or_89 (or_89_out, and_170_out, and_172_out, and_173_out, and_174_out, and_171_out, and_175_out, and_176_out, and_177_out, and_178_out, and_179_out, and_180_out, and_181_out, and_182_out, and_160_out, and_161_out, and_162_out, and_163_out, and_164_out, and_165_out, and_166_out, and_167_out);
  or or_90 (Enable_2A, or_88_out, or_89_out);
  assign RegSel_2A = or_89_out ? DESTREG_2A_2_t : 4'bz;  // Controlled_Buffer controlled_buffer_45
  assign RegSel_2A = or_88_out ? REGSEL_2A_0 : 4'bz;  // Controlled_Buffer controlled_buffer_46
  not not_174 (not_174_out, INSTRUCTION[10]);
  not not_175 (not_175_out, INSTRUCTION[4]);
  not not_176 (not_176_out, INSTRUCTION[4]);
  not not_177 (not_177_out, INSTRUCTION[4]);
  not not_178 (not_178_out, INSTRUCTION[7]);
  not not_179 (not_179_out, INSTRUCTION[7]);
  not not_180 (not_180_out, INSTRUCTION[7]);
  not not_181 (not_181_out, INSTRUCTION[4]);
  not not_182 (not_182_out, INSTRUCTION[4]);
  not not_183 (not_183_out, INSTRUCTION[4]);
  not not_184 (not_184_out, INSTRUCTION[7]);
  not not_185 (not_185_out, INSTRUCTION[7]);
  not not_186 (not_186_out, INSTRUCTION[7]);
  not not_187 (not_187_out, INSTRUCTION[7]);
  not not_188 (not_188_out, INSTRUCTION[7]);
  not not_189 (not_189_out, INSTRUCTION[7]);
  not not_190 (not_190_out, INSTRUCTION[7]);
  not not_191 (not_191_out, INSTRUCTION[7]);
  not not_192 (not_192_out, INSTRUCTION[4]);
  not not_193 (not_193_out, INSTRUCTION[7]);
  not not_194 (not_194_out, INSTRUCTION[7]);
  not not_195 (not_195_out, INSTRUCTION[7]);
  or or_91 (or_91_out, not_184_out, INSTRUCTION[7]);
  or or_92 (or_92_out, Opcode11, Opcode12, Opcode13);
  and and_183 (and_183_out, Opcode18, T4);
  and and_184 (and_184_out, Opcode4, T4);
  and and_185 (and_185_out, Opcode17, T5);
  and and_186 (and_186_out, Opcode17, T6);
  and and_187 (and_187_out, Opcode18, T5);
  buf or_93 (or_93_out, Opcode3);  // OR_Gate
  and and_188 (and_188_out, T4, INSTRUCTION[10], Opcode2);
  and and_189 (and_189_out, T4, not_185_out, INSTRUCTION[10], Opcode2);
  and and_190 (and_190_out, T4, not_186_out, not_174_out, Opcode2);
  and and_191 (and_191_out, T4, INSTRUCTION[7], INSTRUCTION[10], not_176_out, Opcode5);
  and and_192 (and_192_out, T4, not_188_out, INSTRUCTION[10], not_177_out, Opcode6);
  and and_193 (and_193_out, T4, not_178_out, INSTRUCTION[10], INSTRUCTION[4], Opcode6);
  and and_194 (and_194_out, T4, INSTRUCTION[7], INSTRUCTION[10], Opcode7);
  and and_195 (and_195_out, T5, INSTRUCTION[7], INSTRUCTION[10], Opcode7);
  and and_196 (and_196_out, T4, not_179_out, INSTRUCTION[10], Opcode7);
  and and_197 (and_197_out, T5, not_180_out, INSTRUCTION[10], Opcode7);
  and and_198 (and_198_out, T4, INSTRUCTION[7], INSTRUCTION[10], Opcode8);
  and and_199 (and_199_out, T5, INSTRUCTION[7], INSTRUCTION[10], Opcode8);
  and and_200 (and_200_out, T4, not_189_out, INSTRUCTION[10], Opcode8);
  and and_201 (and_201_out, T5, not_190_out, INSTRUCTION[10], Opcode8);
  and and_202 (and_202_out, T4, not_193_out, INSTRUCTION[10], INSTRUCTION[4], Opcode9);
  and and_203 (and_203_out, T4, INSTRUCTION[7], INSTRUCTION[10], not_181_out, Opcode9);
  and and_204 (and_204_out, T5, or_91_out, INSTRUCTION[10], or_92_out);
  not not_196 (not_196_out, Z);
  and and_205 (and_205_out, or_93_out, T4);
  and and_206 (and_206_out, T4, not_187_out, INSTRUCTION[10], not_175_out, Opcode5);
  and and_207 (and_207_out, T4, not_191_out, INSTRUCTION[10], not_192_out, Opcode9);
  and and_208 (and_208_out, T4, not_194_out, INSTRUCTION[10], not_182_out, Opcode10);
  and and_209 (and_209_out, T4, not_195_out, INSTRUCTION[10], INSTRUCTION[4], Opcode10);
  and and_210 (and_210_out, T5, INSTRUCTION[7], INSTRUCTION[10], not_183_out, Opcode10);
  and and_211 (and_211_out, not_196_out, T4, Opcode16);
  and and_212 (and_212_out, Z, T4, Opcode15);
  and and_213 (and_213_out, Opcode14, T4);
  or or_94 (or_94_out, and_213_out, and_211_out, T1, and_212_out, T3);
  buf or_95 (or_95_out, and_205_out);  // OR_Gate
  or or_96 (or_96_out, and_184_out, and_185_out, and_183_out);
  or or_97 (or_97_out, and_186_out, and_187_out);
  or or_98 (or_98_out, and_188_out, and_189_out, and_190_out, and_206_out, and_191_out, and_192_out, and_193_out, and_194_out, and_195_out, and_196_out, and_197_out, and_198_out, and_199_out, and_200_out, and_201_out, and_207_out, and_202_out, and_203_out, and_208_out, and_209_out, and_210_out, and_204_out);
  or or_99 (Enable_2B, or_96_out, or_98_out, or_94_out, or_95_out, or_97_out);
  assign RegSel_2B = or_94_out ? 3'b001 : 3'bz;  // Controlled_Buffer controlled_buffer_47
  assign RegSel_2B = or_97_out ? 3'b001 : 3'bz;  // Controlled_Buffer controlled_buffer_48
  assign RegSel_2B = or_95_out ? 3'b010 : 3'bz;  // Controlled_Buffer controlled_buffer_49
  assign RegSel_2B = or_98_out ? DESTREG_2B_2 : 3'bz;  // Controlled_Buffer controlled_buffer_50
  assign RegSel_2B = or_96_out ? 3'b100 : 3'bz;  // Controlled_Buffer controlled_buffer_51

  // Other names for the same wires on the sheet: IR11 = INSTRUCTION[11]; IR12 = INSTRUCTION[12];
  //   IR13 = INSTRUCTION[13]; IR14 = INSTRUCTION[14]; IR15 = INSTRUCTION[15]; IR8 = INSTRUCTION[8];
  //   IR5 = INSTRUCTION[5]; IR6 = INSTRUCTION[6]; IR9 = INSTRUCTION[9]; IR10 = INSTRUCTION[10]; IR2 = INSTRUCTION[2];
  //   IR3 = INSTRUCTION[3]; IR0 = INSTRUCTION[0]; IR1 = INSTRUCTION[1]; IR4 = INSTRUCTION[4]; IR7 = INSTRUCTION[7]

  // Notes on the sheet:
  //   Opcode
  //   FUNSEL2A
  //   FunSel2b
  //   FunSel ALU
  //   OUTASEL
  //   OUTBSEL
  //   OUTCSEL
  //   MUXA
  //   MUXB
  //   MUXC
  //   REWIND
  //   OUTDSEL
  //   RegSel(2A)
endmodule
