// Logisim project CircularShift.circ as structural Verilog: 1 circuit, main circuit main
module main (
  input  [7:0] IN,
  output CSR_CARRY,
  output CSR_OVERFLOW,
  output CSL_OVERFLOW,
  output CSL_CARRY,
  output [7:0] CSL,
  output [7:0] CSR
);

  Shifter #(.shift("rl")) shifter_1 (.in(IN), .\dist (3'b001), .out(CSL));
  Shifter #(.shift("rr")) shifter_2 (.in(IN), .\dist (3'b001), .out(CSR));
  xor xor_1 (CSR_OVERFLOW, IN[0], IN[7]);
  xor xor_2 (CSL_OVERFLOW, IN[6], IN[7]);

  assign CSL_CARRY = IN[7];
  assign CSR_CARRY = IN[0];
endmodule
