// Logisim project DECODER 6-64.circ as structural Verilog: 1 circuit, main circuit main
module main (
  input  [5:0] INPUT,
  output _0,
  output _1,
  output _2,
  output _3,
  output _4,
  output _5,
  output _6,
  output _7,
  output _8,
  output _9,
  output _10,
  output _11,
  output _12,
  output _13,
  output _14,
  output _15,
  output _16,
  output _17,
  output _18,
  output _19,
  output _20,
  output _21,
  output _22,
  output _23,
  output _24,
  output _25,
  output _26,
  output _27,
  output _28,
  output _29,
  output _30,
  output _31,
  output _32,
  output _33,
  output _34,
  output _35,
  output _36,
  output _37,
  output _38,
  output _39,
  output _40,
  output _41,
  output _42,
  output _43,
  output _44,
  output _45,
  output _46,
  output _47,
  output _48,
  output _49,
  output _50,
  output _51,
  output _52,
  output _53,
  output _54,
  output _55,
  output _56,
  output _57,
  output _58,
  output _59,
  output _60,
  output _61,
  output _62,
  output _63
);

  wire decoder_1_out0, decoder_1_out1, decoder_1_out2, decoder_1_out3;

  Decoder #(.select(2)) decoder_1 (
    .out0(decoder_1_out0), .out1(decoder_1_out1), .out2(decoder_1_out2), .out3(decoder_1_out3),
    .sel(INPUT[5:4]));  // open: en
  Decoder #(.select(4), .disabled(0)) decoder_2 (
    .out0(_0), .out1(_1), .out2(_2), .out3(_3), .out4(_4), .out5(_5), .out6(_6), .out7(_7), .out8(_8),
    .out9(_9), .out10(_10), .out11(_11), .out12(_12), .out13(_13), .out14(_14), .out15(_15),
    .sel(INPUT[3:0]), .en(decoder_1_out0));
  Decoder #(.select(4), .disabled(0)) decoder_3 (
    .out0(_16), .out1(_17), .out2(_18), .out3(_19), .out4(_20), .out5(_21), .out6(_22), .out7(_23),
    .out8(_24), .out9(_25), .out10(_26), .out11(_27), .out12(_28), .out13(_29), .out14(_30), .out15(_31),
    .sel(INPUT[3:0]), .en(decoder_1_out1));
  Decoder #(.select(4), .disabled(0)) decoder_4 (
    .out0(_32), .out1(_33), .out2(_34), .out3(_35), .out4(_36), .out5(_37), .out6(_38), .out7(_39),
    .out8(_40), .out9(_41), .out10(_42), .out11(_43), .out12(_44), .out13(_45), .out14(_46), .out15(_47),
    .sel(INPUT[3:0]), .en(decoder_1_out2));
  Decoder #(.select(4), .disabled(0)) decoder_5 (
    .out0(_48), .out1(_49), .out2(_50), .out3(_51), .out4(_52), .out5(_53), .out6(_54), .out7(_55),
    .out8(_56), .out9(_57), .out10(_58), .out11(_59), .out12(_60), .out13(_61), .out14(_62), .out15(_63),
    .sel(INPUT[3:0]), .en(decoder_1_out3));
endmodule
