// Logisim project LogicalShift.circ as structural Verilog: 1 circuit, main circuit main
module main (
  input  [7:0] IN,
  input  [2:0] DIST,
  input  L_R,
  input  EN,
  output LSR_CARRY,
  output LSL_CARRY,
  output [7:0] out_7
);

  wire [7:0] shifter_1_out, shifter_2_out;

  Shifter shifter_1 (.in(IN), .\dist (DIST), .out(shifter_1_out));
  Shifter #(.shift("lr")) shifter_2 (.in(IN), .\dist (DIST), .out(shifter_2_out));
  Multiplexer #(.width(8)) multiplexer_1 (.in0(shifter_1_out), .in1(shifter_2_out), .out(out_7), .sel(L_R), .en(EN));

  assign LSL_CARRY = IN[7];
  assign LSR_CARRY = IN[0];
endmodule
