// Logisim project PART 2A.circ as structural Verilog: 1 circuit, main circuit main
module main (
  input  clk,
  input  [7:0] I,
  input  [1:0] FunSel,
  input  [1:0] OutASel,
  input  [1:0] OutBSel,
  input  EN,
  input  [3:0] RegSel,
  output [7:0] OutA,
  output [7:0] OutB
);

  wire [3:0] multiplexer_3_out;
  wire [7:0] R0_q, R1_q, R2_q, R3_q;

  REGISTER___8_BIT_main R0 (.I(I), .CLK(clk), .FunSel(FunSel), .E(multiplexer_3_out[0]), .Q(R0_q));
  REGISTER___8_BIT_main R1 (.I(I), .CLK(clk), .FunSel(FunSel), .E(multiplexer_3_out[1]), .Q(R1_q));
  REGISTER___8_BIT_main R2 (.I(I), .CLK(clk), .FunSel(FunSel), .E(multiplexer_3_out[2]), .Q(R2_q));
  REGISTER___8_BIT_main R3 (.I(I), .CLK(clk), .FunSel(FunSel), .E(multiplexer_3_out[3]), .Q(R3_q));
  Multiplexer #(.select(2), .width(8)) multiplexer_1 (
    .in0(R0_q), .in1(R1_q), .in2(R2_q), .in3(R3_q), .out(OutB), .sel(OutBSel), .en(1'b1));
  Multiplexer #(.select(2), .width(8)) multiplexer_2 (
    .in0(R0_q), .in1(R1_q), .in2(R2_q), .in3(R3_q), .out(OutA), .sel(OutASel), .en(1'b1));
  Multiplexer #(.width(4), .enable("false")) multiplexer_3 (
    .in0(RegSel), .in1(4'b0000), .out(multiplexer_3_out), .sel(EN));
endmodule
