// Logisim project PART 2B.circ as structural Verilog: 1 circuit, main circuit main
module main (
  input  CLK,
  input  [7:0] I,
  input  [1:0] OutCSel,
  input  [1:0] OutDSel,
  input  [1:0] FunSel,
  input  EN,
  input  [2:0] RegSel,
  output [7:0] OutC,
  output [7:0] OutD
);

  wire [2:0] multiplexer_3_out;
  wire [7:0] AR_q, PC_q, SP_q;

  Multiplexer #(.select(2), .width(8)) multiplexer_1 (
    .in0(PC_q), .in1(AR_q), .in2(SP_q), .in3(PC_q), .out(OutC), .sel(OutCSel), .en(1'b1));
  REGISTER___8_BIT_main PC (.I(I), .CLK(CLK), .FunSel(FunSel), .E(multiplexer_3_out[0]), .Q(PC_q));
  REGISTER___8_BIT_main AR (.I(I), .CLK(CLK), .FunSel(FunSel), .E(multiplexer_3_out[1]), .Q(AR_q));
  REGISTER___8_BIT_main SP (.I(I), .CLK(CLK), .FunSel(FunSel), .E(multiplexer_3_out[2]), .Q(SP_q));
  Multiplexer #(.select(2), .width(8)) multiplexer_2 (
    .in0(PC_q), .in1(AR_q), .in2(SP_q), .in3(PC_q), .out(OutD), .sel(OutDSel), .en(1'b1));
  Multiplexer #(.width(3), .enable("false")) multiplexer_3 (
    .in0(RegSel), .in1(3'b000), .out(multiplexer_3_out), .sel(EN));
endmodule
