// Logisim project Part1.circ as structural Verilog: 1 circuit, main circuit main
module main (
  input  CLK,
  input  [7:0] A,
  input  [7:0] B,
  input  [3:0] FunSel,
  output [7:0] OutALU,
  output [3:0] OutFlag__ZCNO
);

  wire [3:0] main_1_flags_enable, main_1_outflag__zcno;

  ALU_update_main main_1 (
    .A(A), .B(B), .Cin(OutFlag__ZCNO[2]), .Funsel(FunSel), .OutFlag__ZCNO(main_1_outflag__zcno),
    .OutALU(OutALU), .flags_enable(main_1_flags_enable));
  flag_register_main main_2 (
    .z_input(main_1_outflag__zcno[0]), .c_input(main_1_outflag__zcno[1]), .n_input(main_1_outflag__zcno[2]),
    .o_input(main_1_outflag__zcno[3]), .z_enable(main_1_flags_enable[0]), .c_enable(main_1_flags_enable[1]),
    .n_enable(main_1_flags_enable[2]), .o_enable(main_1_flags_enable[3]), .CLK(CLK),
    .output_flags(OutFlag__ZCNO));
endmodule
