// Logisim project Part2.circ as structural Verilog: 1 circuit, main circuit main
module main (
  input  MuxCSel,
  input  [3:0] FunSel,
  input  [1:0] OutASel,
  input  [1:0] OutBSel,
  input  [1:0] FunSel_2,
  input  [3:0] RegSel,
  input  [1:0] MuxASel,
  input  [1:0] MuxBSel,
  input  [1:0] OutCSel,
  input  str,
  input  ld,
  input  [1:0] OutDSel,
  input  clr,
  input  [1:0] FunSel_3,
  input  [2:0] RegSel_2,
  input  Enable,
  input  [7:0] IR__8_15,
  input  [1:0] FunSel_4,
  input  L_H,
  output [3:0] OutFlag__ZCNO
);

  wire clock_1_out;
  wire [7:0] main_1_outa, main_1_outb, main_2_out, main_3_outalu, main_4_outc, main_4_outd,
       multiplexer_1_out, multiplexer_2_out, multiplexer_3_out, ram_1_data;

  Clock clock_1 (.out(clock_1_out));
  Multiplexer #(.select(2), .width(8), .enable("false")) multiplexer_1 (
    .in0(main_3_outalu), .in1(main_4_outc), .in2(ram_1_data), .in3(main_2_out), .out(multiplexer_1_out),
    .sel(MuxASel));
  PART_2A_main main_1 (
    .I(multiplexer_1_out), .OutA(main_1_outa), .OutB(main_1_outb), .clk(clock_1_out), .OutASel(OutASel),
    .OutBSel(OutBSel), .FunSel(FunSel_2), .RegSel(RegSel));
  Multiplexer #(.select(2), .width(8), .enable("false")) multiplexer_2 (
    .in0({8{1'b0}}), .in1(main_3_outalu), .in2(ram_1_data), .in3(main_2_out), .out(multiplexer_2_out),
    .sel(MuxBSel));
  Multiplexer #(.width(8), .enable("false")) multiplexer_3 (
    .in0(multiplexer_1_out), .in1(main_1_outa), .out(multiplexer_3_out), .sel(MuxCSel));
  PART_2C_main main_2 (
    .CLK(clock_1_out), .EN(Enable), .Funsel(FunSel_4), .IN(ram_1_data), .L_H(L_H),
    .OUT({IR__8_15, main_2_out}));
  Part1_main main_3 (
    .A(multiplexer_3_out), .B(main_1_outb), .FunSel(FunSel), .CLK(clock_1_out), .OutALU(main_3_outalu),
    .OutFlag__ZCNO(OutFlag__ZCNO));
  PART_2B_main main_4 (
    .I(multiplexer_2_out), .OutC(main_4_outc), .OutD(main_4_outd), .CLK(clock_1_out), .OutCSel(OutCSel),
    .OutDSel(OutDSel), .FunSel(FunSel_3), .RegSel(RegSel_2));
  RAM #(.bus("separate")) ram_1 (
    .addr(main_4_outd), .din(main_3_outalu), .data(ram_1_data), .str(str), .sel(1'b1), .clk(clock_1_out),
    .ld(ld), .clr(clr));
endmodule
