// Logisim project REGISTER - 16 BIT.circ as structural Verilog: 1 circuit, main circuit main
module main (
  input  [15:0] I,
  input  CLK,
  input  [1:0] FunSel,
  input  E,
  output [15:0] Q
);

  wire [15:0] main_2_output, main_3_output, multiplexer_1_out;

  Multiplexer #(.select(2), .width(16)) multiplexer_1 (
    .in0({16{1'b0}}), .in1(I), .in2(main_2_output), .in3(main_3_output), .out(multiplexer_1_out),
    .sel(FunSel), .en(E));
  _16bit_D_Latch_main main_1 (.IN(multiplexer_1_out), .CLR(1'b0), .EN(E), .CLK(CLK), .OUT(Q));
  ADDER___16_BIT_main main_2 (.INPUT_1(Q), .INPUT_2(16'h1), .OUTPUT(main_2_output));
  SUBSTRACTOR___16_BIT_main main_3 (.OUTPUT(main_3_output), .INPUT_1(16'h1), .INPUT_2(Q));

  // Notes on the sheet:
  //    D FLIP FLOP
  //   ADDER
  //   SUBTRATCOR
endmodule
