// Logisim project REGISTER - 8 BIT.circ as structural Verilog: 1 circuit, main circuit main
module main (
  input  [7:0] I,
  input  CLK,
  input  [1:0] FunSel,
  input  E,
  output [7:0] Q
);

  wire [7:0] main_2_output, main_3_output, multiplexer_1_out;

  Multiplexer #(.select(2), .width(8)) multiplexer_1 (
    .in0({8{1'b0}}), .in1(I), .in2(main_2_output), .in3(main_3_output), .out(multiplexer_1_out),
    .sel(FunSel), .en(E));
  _8bit_D_Latch_main main_1 (.IN(multiplexer_1_out), .CLR(1'b0), .EN(E), .CLK(CLK), .OUT(Q));
  ADDER___8_BIT_main main_2 (.Input_1(Q), .Input_2(8'h1), .Output(main_2_output));
  SUBTRACTOR___8_BIT_main main_3 (.INPUT_1(Q), .INPUT_2(8'h1), .OUTPUT(main_3_output));

  // Notes on the sheet:
  //   D FLIP FLOP
  //   ADDER
  //   SUBTRACTOR
endmodule
