// Logisim project SUBSTRACTOR - 16 BIT.circ as structural Verilog: 1 circuit, main circuit main
module main (
  input  [15:0] INPUT_1,
  input  [15:0] INPUT_2,
  output [15:0] OUTPUT
);

  wire subtractor_1_bout, subtractor_2_bout, subtractor_3_bout, subtractor_4_bout, subtractor_5_bout,
       subtractor_6_bout, subtractor_7_bout, subtractor_8_bout, subtractor_9_bout, subtractor_10_bout,
       subtractor_11_bout, subtractor_12_bout, subtractor_13_bout, subtractor_14_bout, subtractor_15_bout;

  Subtractor #(.width(1)) subtractor_1 (
    .a(INPUT_1[0]), .b(INPUT_2[0]), .out(OUTPUT[0]), .bout(subtractor_1_bout));  // open: bin
  Subtractor #(.width(1)) subtractor_2 (
    .a(INPUT_1[1]), .b(INPUT_2[1]), .out(OUTPUT[1]), .bin(subtractor_1_bout), .bout(subtractor_2_bout));
  Subtractor #(.width(1)) subtractor_3 (
    .a(INPUT_1[2]), .b(INPUT_2[2]), .out(OUTPUT[2]), .bin(subtractor_2_bout), .bout(subtractor_3_bout));
  Subtractor #(.width(1)) subtractor_4 (
    .a(INPUT_1[3]), .b(INPUT_2[3]), .out(OUTPUT[3]), .bin(subtractor_3_bout), .bout(subtractor_4_bout));
  Subtractor #(.width(1)) subtractor_5 (
    .a(INPUT_1[4]), .b(INPUT_2[4]), .out(OUTPUT[4]), .bin(subtractor_4_bout), .bout(subtractor_5_bout));
  Subtractor #(.width(1)) subtractor_6 (
    .a(INPUT_1[5]), .b(INPUT_2[5]), .out(OUTPUT[5]), .bin(subtractor_5_bout), .bout(subtractor_6_bout));
  Subtractor #(.width(1)) subtractor_7 (
    .a(INPUT_1[6]), .b(INPUT_2[6]), .out(OUTPUT[6]), .bin(subtractor_6_bout), .bout(subtractor_7_bout));
  Subtractor #(.width(1)) subtractor_8 (
    .a(INPUT_1[7]), .b(INPUT_2[7]), .out(OUTPUT[7]), .bin(subtractor_7_bout), .bout(subtractor_8_bout));
  Subtractor #(.width(1)) subtractor_9 (
    .a(INPUT_1[8]), .b(INPUT_2[8]), .out(OUTPUT[8]), .bin(subtractor_8_bout), .bout(subtractor_9_bout));
  Subtractor #(.width(1)) subtractor_10 (
    .a(INPUT_1[9]), .b(INPUT_2[9]), .out(OUTPUT[9]), .bin(subtractor_9_bout), .bout(subtractor_10_bout));
  Subtractor #(.width(1)) subtractor_11 (
    .a(INPUT_1[10]), .b(INPUT_2[10]), .out(OUTPUT[10]), .bin(subtractor_10_bout), .bout(subtractor_11_bout));
  Subtractor #(.width(1)) subtractor_12 (
    .a(INPUT_1[11]), .b(INPUT_2[11]), .out(OUTPUT[11]), .bin(subtractor_11_bout), .bout(subtractor_12_bout));
  Subtractor #(.width(1)) subtractor_13 (
    .a(INPUT_1[12]), .b(INPUT_2[12]), .out(OUTPUT[12]), .bin(subtractor_12_bout), .bout(subtractor_13_bout));
  Subtractor #(.width(1)) subtractor_14 (
    .a(INPUT_1[13]), .b(INPUT_2[13]), .out(OUTPUT[13]), .bin(subtractor_13_bout), .bout(subtractor_14_bout));
  Subtractor #(.width(1)) subtractor_15 (
    .a(INPUT_1[14]), .b(INPUT_2[14]), .out(OUTPUT[14]), .bin(subtractor_14_bout), .bout(subtractor_15_bout));
  Subtractor #(.width(1)) subtractor_16 (
    .a(INPUT_1[15]), .b(INPUT_2[15]), .out(OUTPUT[15]), .bin(subtractor_15_bout));  // open: bout
endmodule
