// Logisim project SUBTRACTOR - 8 BIT.circ as structural Verilog: 1 circuit, main circuit main
module main (
  input  [7:0] INPUT_1,
  input  [7:0] INPUT_2,
  output [7:0] OUTPUT
);

  wire subtractor_1_bout, subtractor_2_bout, subtractor_3_bout, subtractor_4_bout, subtractor_5_bout,
       subtractor_6_bout, subtractor_7_bout;

  Subtractor #(.width(1)) subtractor_1 (
    .a(INPUT_1[0]), .b(INPUT_2[0]), .out(OUTPUT[0]), .bout(subtractor_1_bout));  // open: bin
  Subtractor #(.width(1)) subtractor_2 (
    .a(INPUT_1[1]), .b(INPUT_2[1]), .out(OUTPUT[1]), .bin(subtractor_1_bout), .bout(subtractor_2_bout));
  Subtractor #(.width(1)) subtractor_3 (
    .a(INPUT_1[2]), .b(INPUT_2[2]), .out(OUTPUT[2]), .bin(subtractor_2_bout), .bout(subtractor_3_bout));
  Subtractor #(.width(1)) subtractor_4 (
    .a(INPUT_1[3]), .b(INPUT_2[3]), .out(OUTPUT[3]), .bin(subtractor_3_bout), .bout(subtractor_4_bout));
  Subtractor #(.width(1)) subtractor_5 (
    .a(INPUT_1[4]), .b(INPUT_2[4]), .out(OUTPUT[4]), .bin(subtractor_4_bout), .bout(subtractor_5_bout));
  Subtractor #(.width(1)) subtractor_6 (
    .a(INPUT_1[5]), .b(INPUT_2[5]), .out(OUTPUT[5]), .bin(subtractor_5_bout), .bout(subtractor_6_bout));
  Subtractor #(.width(1)) subtractor_7 (
    .a(INPUT_1[6]), .b(INPUT_2[6]), .out(OUTPUT[6]), .bin(subtractor_6_bout), .bout(subtractor_7_bout));
  Subtractor #(.width(1)) subtractor_8 (
    .a(INPUT_1[7]), .b(INPUT_2[7]), .out(OUTPUT[7]), .bin(subtractor_7_bout));  // open: bout
endmodule
