// Logisim project Shifters.circ as structural Verilog: 1 circuit, main circuit main
module main (
  input  [7:0] IN,
  input  [2:0] SEL,
  input  EN,
  output [7:0] OUT,
  output OFLW,
  output CARRY
);

  wire main_1_lsl_carry, main_1_lsr_carry, main_3_csl_carry, main_3_csr_carry;
  wire [7:0] main_1_lsl, main_1_lsr, main_2_asl, main_2_asr, main_3_csl, main_3_csr;

  LogicalShift_main main_1 (
    .IN(IN), .LSR_CARRY(main_1_lsr_carry), .LSL_CARRY(main_1_lsl_carry), .LSL(main_1_lsl), .LSR(main_1_lsr));
  ArithmeticShift_main main_2 (.IN(IN), .ASL(main_2_asl), .ASR(main_2_asr));
  CircularShift_main main_3 (
    .IN(IN), .CSR_CARRY(main_3_csr_carry), .CSL_CARRY(main_3_csl_carry), .CSL(main_3_csl), .CSR(main_3_csr));  // open: CSR_OVERFLOW, CSL_OVERFLOW
  Multiplexer #(.select(3), .width(8)) multiplexer_1 (
    .in0(main_1_lsl), .in1(main_1_lsr), .in2(main_2_asl), .in3(main_2_asr), .in4(main_3_csl),
    .in5(main_3_csr), .in6({8{1'b0}}), .in7({8{1'b0}}), .out(OUT), .sel(SEL), .en(EN));
  Multiplexer #(.select(3)) multiplexer_2 (
    .in0(main_1_lsl_carry), .in1(main_1_lsr_carry), .in2(1'b0), .in3(1'b0), .in4(main_3_csl_carry),
    .in5(main_3_csr_carry), .in6(1'b0), .in7(1'b0), .out(CARRY), .sel(SEL), .en(EN));
endmodule
