// Logisim project adder.circ as structural Verilog: 1 circuit, main circuit main
module main (
  input  Cin,
  input  [7:0] A,
  input  [7:0] B,
  input  [1:0] Funsel_last2,
  output [7:0] Output,
  output Cout,
  output Overflow
);

  wire adder_1_cout, adder_2_cout, adder_3_cout, adder_4_cout, adder_5_cout, adder_6_cout, adder_7_cout,
       and_1_out, and_2_out, multiplexer_2_out, not_2_out, not_3_out, not_4_out;
  wire [7:0] multiplexer_1_out, not_1_out;

  assign not_1_out = ~B;  // NOT_Gate not_1, 8 bits wide
  Multiplexer #(.select(2), .width(8)) multiplexer_1 (
    .in0(B), .in1(B), .in2(not_1_out), .in3(B), .out(multiplexer_1_out), .sel(Funsel_last2), .en(1'b1));
  Multiplexer #(.select(2)) multiplexer_2 (
    .in0(1'b0), .in1(Cin), .in2(1'b1), .in3(1'b0), .out(multiplexer_2_out), .sel(Funsel_last2), .en(1'b1));
  Adder #(.width(1)) adder_1 (
    .a(A[0]), .b(multiplexer_1_out[0]), .out(Output[0]), .cin(multiplexer_2_out), .cout(adder_1_cout));
  Adder #(.width(1)) adder_2 (
    .a(A[1]), .b(multiplexer_1_out[1]), .out(Output[1]), .cin(adder_1_cout), .cout(adder_2_cout));
  Adder #(.width(1)) adder_3 (
    .a(A[2]), .b(multiplexer_1_out[2]), .out(Output[2]), .cin(adder_2_cout), .cout(adder_3_cout));
  Adder #(.width(1)) adder_4 (
    .a(A[3]), .b(multiplexer_1_out[3]), .out(Output[3]), .cin(adder_3_cout), .cout(adder_4_cout));
  Adder #(.width(1)) adder_5 (
    .a(A[4]), .b(multiplexer_1_out[4]), .out(Output[4]), .cin(adder_4_cout), .cout(adder_5_cout));
  Adder #(.width(1)) adder_6 (
    .a(A[5]), .b(multiplexer_1_out[5]), .out(Output[5]), .cin(adder_5_cout), .cout(adder_6_cout));
  Adder #(.width(1)) adder_7 (
    .a(A[6]), .b(multiplexer_1_out[6]), .out(Output[6]), .cin(adder_6_cout), .cout(adder_7_cout));
  Adder #(.width(1)) adder_8 (.a(A[7]), .b(multiplexer_1_out[7]), .out(Output[7]), .cin(adder_7_cout), .cout(Cout));
  not not_2 (not_2_out, A[7]);
  not not_3 (not_3_out, multiplexer_1_out[7]);
  not not_4 (not_4_out, Output[7]);
  and and_1 (and_1_out, Output[7], not_2_out, not_3_out);
  and and_2 (and_2_out, not_4_out, A[7], multiplexer_1_out[7]);
  or or_1 (Overflow, and_1_out, and_2_out);
endmodule
