// Logisim project adder_update.circ as structural Verilog: 1 circuit, main circuit main
module main (
  input  Cin,
  input  [7:0] A,
  input  [7:0] B,
  input  [1:0] Funsel_last2,
  input  funsell,
  output [7:0] Output,
  output Cout,
  output Overflow
);

  wire adder_1_cout, adder_2_cout, adder_3_cout, adder_4_cout, adder_5_cout, adder_6_cout, adder_7_cout,
       and_1_out, and_2_out, not_1_out, not_2_out, not_3_out, xor_1_out, xor_2_out, xor_3_out, xor_4_out,
       xor_5_out, xor_6_out, xor_7_out, xor_8_out;

  xor xor_1 (xor_1_out, funsell, B[0]);
  xor xor_2 (xor_2_out, funsell, B[1]);
  xor xor_3 (xor_3_out, funsell, B[2]);
  xor xor_4 (xor_4_out, funsell, B[3]);
  xor xor_5 (xor_5_out, funsell, B[4]);
  xor xor_6 (xor_6_out, funsell, B[5]);
  xor xor_7 (xor_7_out, funsell, B[6]);
  xor xor_8 (xor_8_out, funsell, B[7]);
  Adder #(.width(1)) adder_1 (.a(A[0]), .b(xor_1_out), .out(Output[0]), .cin(Cin), .cout(adder_1_cout));
  Adder #(.width(1)) adder_2 (.a(A[1]), .b(xor_2_out), .out(Output[1]), .cin(adder_1_cout), .cout(adder_2_cout));
  Adder #(.width(1)) adder_3 (.a(A[2]), .b(xor_3_out), .out(Output[2]), .cin(adder_2_cout), .cout(adder_3_cout));
  Adder #(.width(1)) adder_4 (.a(A[3]), .b(xor_4_out), .out(Output[3]), .cin(adder_3_cout), .cout(adder_4_cout));
  Adder #(.width(1)) adder_5 (.a(A[4]), .b(xor_5_out), .out(Output[4]), .cin(adder_4_cout), .cout(adder_5_cout));
  Adder #(.width(1)) adder_6 (.a(A[5]), .b(xor_6_out), .out(Output[5]), .cin(adder_5_cout), .cout(adder_6_cout));
  Adder #(.width(1)) adder_7 (.a(A[6]), .b(xor_7_out), .out(Output[6]), .cin(adder_6_cout), .cout(adder_7_cout));
  Adder #(.width(1)) adder_8 (.a(A[7]), .b(xor_8_out), .out(Output[7]), .cin(adder_7_cout), .cout(Cout));
  not not_1 (not_1_out, A[7]);
  not not_2 (not_2_out, xor_8_out);
  not not_3 (not_3_out, Output[7]);
  and and_1 (and_1_out, Output[7], not_1_out, not_2_out);
  and and_2 (and_2_out, not_3_out, A[7], xor_8_out);
  or or_1 (Overflow, and_1_out, and_2_out);
endmodule
