// Logisim project flag_register.circ as structural Verilog: 1 circuit, main circuit main
module main (
  input  CLK,
  input  z_input,
  input  c_input,
  input  n_input,
  input  o_input,
  input  z_enable,
  input  c_enable,
  input  n_enable,
  input  o_enable,
  output [3:0] output_flags
);

  D_Flip_Flop d_ff_1 (.clk(CLK), .D(z_input), .Q(output_flags[3]), .en(z_enable));  // open: Qn, preset, reset
  D_Flip_Flop d_ff_2 (.clk(CLK), .D(c_input), .Q(output_flags[2]), .en(c_enable));  // open: Qn, preset, reset
  D_Flip_Flop d_ff_3 (.clk(CLK), .D(n_input), .Q(output_flags[1]), .en(n_enable));  // open: Qn, preset, reset
  D_Flip_Flop d_ff_4 (.clk(CLK), .D(o_input), .Q(output_flags[0]), .en(o_enable));  // open: Qn, preset, reset
endmodule
