// Logisim project logic_and_arithmetic.circ as structural Verilog: 1 circuit, main circuit main
module main (
  input  [7:0] A,
  input  [7:0] B,
  input  [3:0] Funsel,
  input  Cin,
  input  EN,
  output [7:0] out_6
);

  wire [7:0] and_1_out, main_1_output, not_1_out, not_2_out, or_1_out, xor_1_out;

  assign not_1_out = ~A;  // NOT_Gate not_1, 8 bits wide
  assign and_1_out = A & B;  // AND_Gate and_1, 8 bits wide
  assign or_1_out = A | B;  // OR_Gate or_1, 8 bits wide
  assign not_2_out = ~B;  // NOT_Gate not_2, 8 bits wide
  assign xor_1_out = B ^ A;  // XOR_Gate xor_1, 8 bits wide
  adder_main main_1 (
    .A(A), .B(B), .Funsel_last2(Funsel[1:0]), .Cin(Cin), .EN(EN), .Output(main_1_output));  // open: Cout, Overflow
  Multiplexer #(.select(4), .width(8)) multiplexer_1 (
    .in0(A), .in1(B), .in2(not_1_out), .in3(not_2_out), .in4(main_1_output), .in5(main_1_output),
    .in6(main_1_output), .in7(and_1_out), .in8(or_1_out), .in9(xor_1_out), .out(out_6), .sel(Funsel), .en(EN));  // open: in10, in11, in12, in13, in14, in15
endmodule
