// Logisim project micro-programmed-CU.circ as structural Verilog: 1 circuit, main circuit main
module main (
  input  [15:0] IR
);

  wire decoder_2_out0, decoder_2_out1, decoder_4_out0, decoder_4_out1, decoder_8_out0, decoder_8_out1,
       not_1_out, not_2_out, not_3_out, Opcode0, Opcode1, Opcode2, Opcode3, Opcode4, Opcode5, Opcode6,
       Opcode7, Opcode8, Opcode9, Opcode10, Opcode11, Opcode12, Opcode13, Opcode14, Opcode15, Opcode16,
       Opcode17, Opcode18, or_4_out, or_5_out;
  wire [2:0] DESTREG_2B_2, SRCREG1_2B_2, SRCREG2_2B_2;
  wire [3:0] DESTREG_2A_2, MAP, REGSEL_2A_0, SRCREG1_2A_2, SRCREG2_2A_2;

  not not_1 (not_1_out, IR[10]);
  not not_2 (not_2_out, IR[4]);
  Decoder #(.select(2)) decoder_1 (
    .out0(DESTREG_2A_2[0]), .out1(DESTREG_2A_2[1]), .out2(DESTREG_2A_2[2]), .out3(DESTREG_2A_2[3]),
    .sel(IR[9:8]), .en(not_1_out));
  Decoder #(.select(2)) decoder_2 (
    .out0(decoder_2_out0), .out1(decoder_2_out1), .out2(DESTREG_2B_2[1]), .out3(DESTREG_2B_2[2]),
    .sel(IR[9:8]), .en(IR[10]));
  or or_1 (DESTREG_2B_2[0], decoder_2_out0, decoder_2_out1);
  Decoder #(.select(2)) decoder_3 (
    .out0(SRCREG2_2A_2[0]), .out1(SRCREG2_2A_2[1]), .out2(SRCREG2_2A_2[2]), .out3(SRCREG2_2A_2[3]),
    .sel(IR[3:2]), .en(not_2_out));
  Decoder #(.select(2)) decoder_4 (
    .out0(decoder_4_out0), .out1(decoder_4_out1), .out2(SRCREG2_2B_2[1]), .out3(SRCREG2_2B_2[2]),
    .sel(IR[3:2]), .en(IR[4]));
  or or_2 (SRCREG2_2B_2[0], decoder_4_out0, decoder_4_out1);
  Decoder #(.select(5)) decoder_5 (
    .out0(Opcode0), .out1(Opcode1), .out2(Opcode2), .out3(Opcode3), .out4(Opcode4), .out5(Opcode5),
    .out6(Opcode6), .out7(Opcode7), .out8(Opcode8), .out9(Opcode9), .out10(Opcode10), .out11(Opcode11),
    .out12(Opcode12), .out13(Opcode13), .out14(Opcode14), .out15(Opcode15), .out16(Opcode16),
    .out17(Opcode17), .out18(Opcode18), .sel(IR[15:11]));  // open: out19, out20, out21, out22, out23, out24, out25, out26, out27, out28, out29, out30, out31, en
  Decoder #(.select(2), .enable("false")) decoder_6 (
    .out0(REGSEL_2A_0[0]), .out1(REGSEL_2A_0[1]), .out2(REGSEL_2A_0[2]), .out3(REGSEL_2A_0[3]), .sel(IR[10:9]));
  not not_3 (not_3_out, IR[7]);
  Decoder #(.select(2)) decoder_7 (
    .out0(SRCREG1_2A_2[0]), .out1(SRCREG1_2A_2[1]), .out2(SRCREG1_2A_2[2]), .out3(SRCREG1_2A_2[3]),
    .sel(IR[6:5]), .en(not_3_out));
  Decoder #(.select(2)) decoder_8 (
    .out0(decoder_8_out0), .out1(decoder_8_out1), .out2(SRCREG1_2B_2[1]), .out3(SRCREG1_2B_2[2]),
    .sel(IR[6:5]), .en(IR[7]));
  or or_3 (SRCREG1_2B_2[0], decoder_8_out0, decoder_8_out1);
  Multiplexer multiplexer_1 (.in0(1'b0), .in1(IR[10]), .out(MAP[3]), .sel(or_4_out));  // open: en
  Multiplexer multiplexer_2 (.in0(1'b0), .in1(IR[8]), .out(MAP[2]), .sel(Opcode0));  // open: en
  Multiplexer multiplexer_3 (.in0(1'b0), .in1(IR[7]), .out(MAP[1]), .sel(or_4_out));  // open: en
  or or_4 (or_4_out, Opcode2, Opcode5, Opcode6, Opcode7, Opcode8, Opcode9, Opcode10, Opcode11, Opcode12, Opcode13);
  or or_5 (or_5_out, Opcode5, Opcode6, Opcode9, Opcode10);
  Multiplexer multiplexer_4 (.in0(1'b0), .in1(IR[4]), .out(MAP[0]), .sel(or_5_out));  // open: en

  // Other names for the same wires on the sheet: MAP[8:4] = IR[15:11]
endmodule
