// Logisim project microop decoder.circ as structural Verilog: 1 circuit, main circuit main
module main (
  input  [15:0] IR,
  input  [5:0] MicroOp,
  input  CLK,
  input  Z,
  output [3:0] FunSel_ALU,
  output READ,
  output LOAD,
  output EN_RAM,
  output MUXCSEL,
  output [1:0] MUXBSEL,
  output [1:0] MUXASEL,
  output [1:0] FUNSEL_2B,
  output EN_2B,
  output [1:0] FUNSEL_2A,
  output EN_2A,
  output LH,
  output [1:0] FUNSEL_2C,
  output EN_2C
);

  wire decoder_2_out0, decoder_2_out1, decoder_6_out0, decoder_6_out1, decoder_8_out0, decoder_8_out1,
       not_1_out, not_2_out, not_3_out, OP0, OP1, OP2, OP3, OP4, OP5, OP6, OP7, OP8, OP9, OP10, OP11, OP12,
       OP13, OP14, OP15, OP16, OP17, OP18, OP19, OP20, OP21, OP22, OP23, OP24, OP25, OP26, OP27, OP28, OP29,
       OP30, OP31, OP32, OP33, OP34, OP35, OP36, OP37, OP38, OP39, OP40, OP41, OP42, OP43, OP44, OP45, OP46,
       OP47, OP48, OP49, OP50, OP51, OP52, OP53, OP54, OP55, OP56, OP57, OP58, OP59, OP60, OP61, OP62, OP63,
       Opcode0, Opcode1, Opcode2, Opcode3, Opcode4, Opcode5, Opcode6, Opcode7, Opcode8, Opcode9, Opcode10,
       Opcode11, Opcode12, Opcode13, Opcode14, Opcode15, Opcode16, Opcode17, Opcode18, or_4_out, or_5_out,
       or_6_out;
  wire [1:0] controlled_buffer_1_out;
  wire [2:0] DESTREG_2B_2, SRCREG1_2B_2, SRCREG2_2B_2;
  wire [3:0] DESTREG_2A_2, REGSEL_2A_0, SRCREG1_2A_2, SRCREG2_2A_2;
  wire [5:0] MicroOps;
  wire [8:5] MAP;

  not not_1 (not_1_out, IR[10]);
  Decoder #(.select(5)) decoder_1 (
    .out0(Opcode0), .out1(Opcode1), .out2(Opcode2), .out3(Opcode3), .out4(Opcode4), .out5(Opcode5),
    .out6(Opcode6), .out7(Opcode7), .out8(Opcode8), .out9(Opcode9), .out10(Opcode10), .out11(Opcode11),
    .out12(Opcode12), .out13(Opcode13), .out14(Opcode14), .out15(Opcode15), .out16(Opcode16),
    .out17(Opcode17), .out18(Opcode18), .sel(IR[15:11]));  // open: out19, out20, out21, out22, out23, out24, out25, out26, out27, out28, out29, out30, out31, en
  Decoder #(.select(2)) decoder_2 (
    .out0(decoder_2_out0), .out1(decoder_2_out1), .out2(DESTREG_2B_2[1]), .out3(DESTREG_2B_2[2]),
    .sel(IR[9:8]), .en(IR[10]));
  or or_1 (DESTREG_2B_2[0], decoder_2_out0, decoder_2_out1);
  Decoder #(.select(2)) decoder_3 (
    .out0(DESTREG_2A_2[0]), .out1(DESTREG_2A_2[1]), .out2(DESTREG_2A_2[2]), .out3(DESTREG_2A_2[3]),
    .sel(IR[9:8]), .en(not_1_out));
  Decoder #(.select(2), .enable("false")) decoder_4 (
    .out0(REGSEL_2A_0[0]), .out1(REGSEL_2A_0[1]), .out2(REGSEL_2A_0[2]), .out3(REGSEL_2A_0[3]), .sel(IR[10:9]));
  not not_2 (not_2_out, IR[7]);
  or or_2 (SRCREG1_2B_2[0], decoder_6_out0, decoder_6_out1);
  not not_3 (not_3_out, IR[4]);
  or or_3 (SRCREG2_2B_2[0], decoder_8_out0, decoder_8_out1);
  Decoder #(.select(2)) decoder_5 (
    .out0(SRCREG1_2A_2[0]), .out1(SRCREG1_2A_2[1]), .out2(SRCREG1_2A_2[2]), .out3(SRCREG1_2A_2[3]),
    .sel(IR[6:5]), .en(not_2_out));
  Decoder #(.select(2)) decoder_6 (
    .out0(decoder_6_out0), .out1(decoder_6_out1), .out2(SRCREG1_2B_2[1]), .out3(SRCREG1_2B_2[2]),
    .sel(IR[6:5]), .en(IR[7]));
  Decoder #(.select(2)) decoder_7 (
    .out0(SRCREG2_2A_2[0]), .out1(SRCREG2_2A_2[1]), .out2(SRCREG2_2A_2[2]), .out3(SRCREG2_2A_2[3]),
    .sel(IR[3:2]), .en(not_3_out));
  Decoder #(.select(2)) decoder_8 (
    .out0(decoder_8_out0), .out1(decoder_8_out1), .out2(SRCREG2_2B_2[1]), .out3(SRCREG2_2B_2[2]),
    .sel(IR[3:2]), .en(IR[4]));
  sequencer_main main_1 (
    .CLK(CLK), .MAP({1'b1, MAP, IR[11], IR[12], IR[13], IR[14], IR[15]}), .Z(Z), .MicroOp(MicroOps));
  Multiplexer multiplexer_1 (.in0(1'b0), .in1(IR[10]), .out(MAP[5]), .sel(or_5_out));  // open: en
  Multiplexer multiplexer_2 (.in0(1'b0), .in1(IR[8]), .out(MAP[6]), .sel(Opcode0));  // open: en
  or or_4 (or_4_out, Opcode5, Opcode6, Opcode9, Opcode10);
  Multiplexer multiplexer_3 (.in0(1'b0), .in1(IR[7]), .out(MAP[7]), .sel(or_5_out));  // open: en
  or or_5 (or_5_out, Opcode2, Opcode5, Opcode6, Opcode7, Opcode8, Opcode9, Opcode10, Opcode11, Opcode12, Opcode13);
  Multiplexer multiplexer_4 (.in0(1'b0), .in1(IR[4]), .out(MAP[8]), .sel(or_4_out));  // open: en
  DECODER_6_64_main main_2 (
    .INPUT(MicroOps), ._0(OP0), ._1(OP1), ._2(OP2), ._3(OP3), ._4(OP4), ._5(OP5), ._6(OP6), ._7(OP7),
    ._8(OP8), ._9(OP9), ._10(OP10), ._11(OP11), ._12(OP12), ._13(OP13), ._14(OP14), ._15(OP15), ._16(OP16),
    ._17(OP17), ._18(OP18), ._19(OP19), ._20(OP20), ._21(OP21), ._22(OP22), ._23(OP23), ._24(OP24),
    ._25(OP25), ._26(OP26), ._27(OP27), ._28(OP28), ._29(OP29), ._30(OP30), ._31(OP31), ._32(OP32),
    ._33(OP33), ._34(OP34), ._35(OP35), ._36(OP36), ._37(OP37), ._38(OP38), ._39(OP39), ._40(OP40),
    ._41(OP41), ._42(OP42), ._43(OP43), ._44(OP44), ._45(OP45), ._46(OP46), ._47(OP47), ._48(OP48),
    ._49(OP49), ._50(OP50), ._51(OP51), ._52(OP52), ._53(OP53), ._54(OP54), ._55(OP55), ._56(OP56),
    ._57(OP57), ._58(OP58), ._59(OP59), ._60(OP60), ._61(OP61), ._62(OP62), ._63(OP63));
  ROM #(.addrWidth(6), .dataWidth(22)) rom_1 (
    .addr(MicroOp),
    .data({EN_2C, FUNSEL_2C, LH, EN_2A, FUNSEL_2A, EN_2B, FUNSEL_2B, MUXASEL, MUXBSEL, MUXCSEL, EN_RAM, LOAD, READ, FunSel_ALU}));  // open: sel
  or or_6 (or_6_out, OP2, OP2);
  assign controlled_buffer_1_out = or_6_out ? 2'b01 : 2'bz;  // Controlled_Buffer controlled_buffer_1

  // Other names for the same wires on the sheet: MAP[4:0] = {IR[11], IR[12], IR[13], IR[14], IR[15]}
endmodule
