// Logisim project outasel-outbsel-outcsel (serhat).circ as structural Verilog: 1 circuit, main circuit OUTASEL
module OUTASEL (
  input  [1:0] OUTASEL,
  input  [1:0] OUTBSEL,
  input  [1:0] OUTCSEL
);

  wire and_1_out, and_2_out, and_3_out, and_4_out, and_5_out, and_6_out, and_7_out, and_8_out, and_9_out,
       and_10_out, and_11_out, and_12_out, and_13_out, and_14_out, and_15_out, and_16_out, and_17_out,
       and_18_out, and_19_out, and_20_out, and_21_out, and_22_out, and_23_out, and_24_out, and_25_out,
       and_26_out, and_27_out, and_28_out, and_29_out, and_30_out, and_31_out, and_32_out, and_33_out, IR2,
       IR3, IR4, IR5, IR6, IR7, IR8, IR9, IR10, not_1_out, not_3_out, not_4_out, not_6_out, not_7_out,
       not_8_out, not_9_out, not_10_out, not_12_out, not_13_out, not_14_out, not_15_out, not_16_out,
       not_17_out, not_18_out, not_19_out, not_20_out, not_21_out, not_22_out, not_23_out, not_24_out,
       not_25_out, not_26_out, not_27_out, not_28_out, not_29_out, not_30_out, not_31_out, not_32_out,
       Opcode0, Opcode1, Opcode2, Opcode5, Opcode6, Opcode7, Opcode8, Opcode9, Opcode10, Opcode11, Opcode12,
       Opcode13, Opcode17, or_1_out, or_2_out, or_3_out, or_4_out, or_5_out, or_6_out, or_7_out, or_8_out,
       or_9_out, or_10_out, or_11_out, or_12_out, or_13_out, or_14_out, or_15_out, or_16_out, or_17_out,
       or_18_out, or_19_out, or_20_out, or_21_out, T0, T1, T2, T4, T5, T6;
  wire [1:0] DESTREG_2B_2, SRCREG1_2A_2, SRCREG1_2B_2, SRCREG2_2A_2, SRCREG2_2B_2;

  not not_1 (not_1_out, IR10);
  not not_2 (Opcode8, IR7);
  or or_1 (or_1_out, Opcode9, Opcode10);
  or or_2 (or_2_out, Opcode11, Opcode12, Opcode13);
  not not_3 (not_3_out, IR8);
  not not_4 (not_4_out, IR8);
  not not_5 (Opcode5, IR4);
  not not_6 (not_6_out, IR10);
  not not_7 (not_7_out, IR4);
  not not_8 (not_8_out, IR7);
  not not_9 (not_9_out, IR7);
  and and_1 (and_1_out, not_3_out, Opcode0, T5);
  and and_2 (and_2_out, IR8, Opcode0, T4);
  and and_3 (and_3_out, Opcode1, T4);
  and and_4 (and_4_out, not_4_out, Opcode5, Opcode5, T4);
  and and_5 (and_5_out, not_6_out, Opcode7, Opcode7, T6);
  and and_6 (and_6_out, not_1_out, Opcode8, Opcode8, T6);
  not not_10 (not_10_out, IR4);
  not not_11 (Opcode5, IR7);
  and and_7 (and_7_out, not_9_out, or_2_out, T4);
  and and_8 (and_8_out, not_7_out, not_8_out, or_1_out, T4);
  or or_3 (or_3_out, and_1_out, and_2_out, and_3_out);
  or or_4 (or_4_out, and_4_out, and_5_out, and_6_out);
  and and_9 (and_9_out, not_10_out, Opcode5, Opcode5, T4);
  assign OUTASEL = and_9_out ? SRCREG2_2A_2 : 2'bz;  // Controlled_Buffer controlled_buffer_1
  or or_5 (or_5_out, and_8_out, and_7_out);
  assign OUTASEL = or_3_out ? {IR9, IR10} : 2'bz;  // Controlled_Buffer controlled_buffer_2
  assign OUTASEL = or_4_out ? {IR5, IR6} : 2'bz;  // Controlled_Buffer controlled_buffer_3
  assign OUTASEL = or_5_out ? SRCREG1_2A_2 : 2'bz;  // Controlled_Buffer controlled_buffer_4
  or or_6 (or_6_out, Opcode9, Opcode10);
  not not_12 (not_12_out, IR7);
  or or_7 (or_7_out, Opcode9, Opcode10);
  not not_13 (not_13_out, IR4);
  not not_14 (not_14_out, IR7);
  not not_15 (not_15_out, IR10);
  not not_16 (not_16_out, IR4);
  not not_17 (not_17_out, IR4);
  not not_18 (not_18_out, IR7);
  not not_19 (not_19_out, IR10);
  not not_20 (not_20_out, IR7);
  not not_21 (not_21_out, IR4);
  or or_8 (or_8_out, Opcode9, Opcode10);
  and and_10 (and_10_out, T4, not_14_out, Opcode5);
  and and_11 (and_11_out, T4, not_16_out, Opcode5);
  and and_12 (and_12_out, T4, not_17_out, Opcode5);
  and and_13 (and_13_out, T4, not_18_out, Opcode6);
  not not_22 (not_22_out, IR7);
  or or_9 (or_9_out, Opcode2, Opcode7, Opcode8);
  not not_23 (not_23_out, IR4);
  not not_24 (not_24_out, IR7);
  and and_14 (and_14_out, T4, not_21_out, not_12_out, or_7_out);
  and and_15 (and_15_out, T4, IR7, not_13_out, or_8_out);
  and and_16 (and_16_out, T5, not_19_out, IR7, Opcode5);
  and and_17 (and_17_out, T4, not_22_out, or_9_out);
  and and_18 (and_18_out, T4, not_24_out, Opcode6);
  and and_19 (and_19_out, T4, not_20_out, or_6_out);
  or or_10 (or_10_out, and_14_out, and_15_out);
  or or_11 (or_11_out, and_10_out, and_11_out);
  assign OUTBSEL = or_11_out ? {IR2, IR3} : 2'bz;  // Controlled_Buffer controlled_buffer_5
  or or_12 (or_12_out, and_12_out, and_13_out);
  assign OUTBSEL = or_12_out ? {IR5, IR6} : 2'bz;  // Controlled_Buffer controlled_buffer_6
  assign OUTBSEL = and_16_out ? {IR9, IR10} : 2'bz;  // Controlled_Buffer controlled_buffer_7
  or or_13 (or_13_out, and_17_out, and_18_out, and_19_out);
  assign OUTBSEL = or_10_out ? SRCREG2_2A_2 : 2'bz;  // Controlled_Buffer controlled_buffer_8
  assign OUTBSEL = or_13_out ? SRCREG1_2A_2 : 2'bz;  // Controlled_Buffer controlled_buffer_9
  not not_25 (not_25_out, IR7);
  not not_26 (not_26_out, IR10);
  not not_27 (not_27_out, IR7);
  not not_28 (not_28_out, IR10);
  not not_29 (not_29_out, IR4);
  not not_30 (not_30_out, IR7);
  or or_14 (or_14_out, Opcode8, Opcode7);
  or or_15 (or_15_out, Opcode9, Opcode10);
  not not_31 (not_31_out, IR4);
  not not_32 (not_32_out, IR4);
  or or_16 (or_16_out, Opcode9, Opcode10);
  or or_17 (or_17_out, Opcode11, Opcode12, Opcode13);
  and and_20 (and_20_out, T5, IR4, IR7, not_26_out, Opcode5);
  and and_21 (and_21_out, T4, IR7, Opcode2);
  and and_22 (and_22_out, T4, IR4, not_28_out, Opcode5);
  and and_23 (and_23_out, T4, not_31_out, IR7, Opcode5);
  and and_24 (and_24_out, T4, not_29_out, IR7, or_16_out);
  and and_25 (and_25_out, T4, IR7, or_17_out);
  and and_26 (and_26_out, T4, IR4, not_30_out, IR10, Opcode6);
  and and_27 (and_27_out, T4, IR7, or_14_out);
  and and_28 (and_28_out, T4, IR4, not_25_out, or_15_out);
  and and_29 (and_29_out, T6, IR10, Opcode7);
  and and_30 (and_30_out, T6, IR7, Opcode8);
  and and_31 (and_31_out, T6, IR10, not_27_out, Opcode8);
  and and_32 (and_32_out, T4, Opcode17);
  and and_33 (and_33_out, T4, not_32_out, IR7, IR10, Opcode6);
  or or_18 (or_18_out, and_26_out, and_27_out, and_28_out, and_20_out);
  or or_19 (or_19_out, and_29_out, and_30_out, and_31_out);
  assign OUTCSEL = or_19_out ? DESTREG_2B_2 : 2'bz;  // Controlled_Buffer controlled_buffer_10
  or or_20 (or_20_out, and_32_out, T0, T1, T2);
  or or_21 (or_21_out, and_21_out, and_22_out, and_23_out, and_33_out, and_24_out, and_25_out);
  assign OUTCSEL = or_18_out ? SRCREG2_2B_2 : 2'bz;  // Controlled_Buffer controlled_buffer_11
  assign OUTCSEL = or_20_out ? 2'b00 : 2'bz;  // Controlled_Buffer controlled_buffer_12
  assign OUTCSEL = or_21_out ? SRCREG1_2B_2 : 2'bz;  // Controlled_Buffer controlled_buffer_13

  // Notes on the sheet:
  //   OUTASEL
  //   OUTBSEL
  //   OUTCSEL
endmodule
