// Logisim project outdsel.circ as structural Verilog: 1 circuit, main circuit main
module main (
  output [1:0] out_1
);

  wire and_1_out, and_2_out, and_3_out, and_4_out, and_5_out, and_6_out, IR8, not_1_out, Opcode0, Opcode1,
       Opcode4, Opcode17, Opcode18, or_1_out, or_2_out, T4, T5;

  not not_1 (not_1_out, IR8);
  and and_1 (and_1_out, Opcode0, not_1_out, T5);
  and and_2 (and_2_out, Opcode0, IR8, T4);
  and and_3 (and_3_out, Opcode1, T5);
  and and_4 (and_4_out, Opcode4, T5);
  and and_5 (and_5_out, Opcode17, T4);
  and and_6 (and_6_out, Opcode18, T4);
  or or_1 (or_1_out, and_1_out, and_2_out, and_3_out);
  or or_2 (or_2_out, and_4_out, and_5_out, and_6_out);
  assign out_1 = or_1_out ? 2'b01 : 2'bz;  // Controlled_Buffer controlled_buffer_1
  assign out_1 = or_2_out ? 2'b10 : 2'bz;  // Controlled_Buffer controlled_buffer_2
endmodule
