// Logisim project regsel2a.circ as structural Verilog: 1 circuit, main circuit main
module main (
  output [3:0] EN
);

  wire and_1_out, and_2_out, and_3_out, and_4_out, and_5_out, and_6_out, and_7_out, and_8_out, and_9_out,
       and_10_out, and_11_out, and_12_out, and_13_out, and_14_out, and_15_out, and_16_out, and_17_out,
       and_18_out, and_19_out, and_20_out, and_21_out, and_22_out, and_23_out, IR4, IR7, IR8, IR10,
       not_1_out, not_2_out, not_3_out, not_4_out, not_5_out, not_6_out, not_7_out, not_8_out, not_9_out,
       not_10_out, not_11_out, not_12_out, not_13_out, not_14_out, not_15_out, not_16_out, not_17_out,
       not_18_out, not_19_out, not_20_out, not_21_out, not_22_out, not_23_out, not_24_out, not_25_out,
       not_26_out, not_27_out, not_28_out, not_29_out, not_30_out, not_31_out, not_32_out, not_33_out,
       not_34_out, not_35_out, not_36_out, not_37_out, Opcode0, Opcode1, Opcode2, Opcode4, Opcode7, Opcode8,
       Opcode9, Opcode10, Opcode11, Opcode12, Opcode13, or_1_out, or_2_out, T4, T5;
  wire [3:0] DESTREG_2A_2, REGSEL_2A_0;

  not not_1 (not_1_out, IR10);
  not not_2 (not_2_out, IR7);
  not not_3 (not_3_out, IR4);
  not not_4 (not_4_out, IR10);
  not not_5 (not_5_out, IR7);
  not not_6 (not_6_out, IR10);
  not not_7 (not_7_out, IR4);
  not not_8 (not_8_out, IR10);
  not not_9 (not_9_out, IR7);
  not not_10 (not_10_out, IR4);
  not not_11 (not_11_out, IR10);
  not not_12 (not_12_out, IR7);
  not not_13 (not_13_out, IR10);
  not not_14 (not_14_out, IR4);
  not not_15 (not_15_out, IR10);
  not not_16 (not_16_out, IR7);
  not not_17 (not_17_out, IR10);
  not not_18 (not_18_out, IR10);
  not not_19 (not_19_out, IR7);
  not not_20 (not_20_out, IR10);
  not not_21 (not_21_out, IR10);
  not not_22 (not_22_out, IR7);
  not not_23 (not_23_out, IR10);
  not not_24 (not_24_out, IR8);
  not not_25 (not_25_out, IR10);
  not not_26 (not_26_out, IR10);
  not not_27 (not_27_out, IR7);
  not not_28 (not_28_out, IR10);
  not not_29 (not_29_out, IR10);
  not not_30 (not_30_out, IR7);
  not not_31 (not_31_out, IR10);
  not not_32 (not_32_out, IR7);
  not not_33 (not_33_out, IR10);
  not not_34 (not_34_out, IR10);
  not not_35 (not_35_out, IR7);
  not not_36 (not_36_out, IR10);
  not not_37 (not_37_out, IR7);
  and and_1 (and_1_out, not_15_out, Opcode11, not_16_out, T5);
  and and_2 (and_2_out, not_17_out, Opcode11, IR7, T5);
  and and_3 (and_3_out, not_18_out, Opcode12, not_19_out, T5);
  and and_4 (and_4_out, not_21_out, Opcode13, not_22_out, T5);
  and and_5 (and_5_out, not_23_out, Opcode13, IR7, T5);
  and and_6 (and_6_out, not_24_out, Opcode0, T5);
  and and_7 (and_7_out, Opcode1, T4);
  and and_8 (and_8_out, Opcode4, T5);
  and and_9 (and_9_out, not_25_out, Opcode2, IR7, T4);
  and and_10 (and_10_out, not_26_out, Opcode2, not_27_out, T4);
  and and_11 (and_11_out, not_28_out, Opcode7, IR7, T4);
  and and_12 (and_12_out, not_29_out, Opcode7, not_30_out, T4);
  and and_13 (and_13_out, not_31_out, Opcode7, not_32_out, T5);
  and and_14 (and_14_out, not_33_out, Opcode8, IR7, T4);
  and and_15 (and_15_out, not_34_out, Opcode8, not_35_out, T4);
  and and_16 (and_16_out, not_36_out, Opcode8, not_37_out, T5);
  and and_17 (and_17_out, not_1_out, Opcode9, not_3_out, not_2_out, T4);
  and and_18 (and_18_out, not_4_out, Opcode9, IR4, not_5_out, T5);
  and and_19 (and_19_out, not_6_out, Opcode9, not_7_out, IR7, T5);
  and and_20 (and_20_out, not_8_out, Opcode10, not_10_out, not_9_out, T4);
  and and_21 (and_21_out, not_11_out, Opcode10, IR4, not_12_out, T5);
  and and_22 (and_22_out, not_13_out, Opcode10, not_14_out, IR7, T5);
  and and_23 (and_23_out, not_20_out, Opcode12, IR7, T5);
  or or_1 (or_1_out, and_6_out, and_7_out, and_8_out);
  or or_2 (or_2_out, and_9_out, and_11_out, and_12_out, and_13_out, and_10_out, and_14_out, and_15_out, and_16_out, and_17_out, and_18_out, and_19_out, and_20_out, and_21_out, and_22_out, and_1_out, and_2_out, and_3_out, and_23_out, and_4_out, and_5_out);
  assign EN = or_1_out ? REGSEL_2A_0 : 4'bz;  // Controlled_Buffer controlled_buffer_1
  assign EN = or_2_out ? DESTREG_2A_2 : 4'bz;  // Controlled_Buffer controlled_buffer_2
endmodule
