// Logisim project regsel2b.circ as structural Verilog: 1 circuit, main circuit main
module main (
  input  [2:0] EN
);

  wire and_1_out, and_2_out, and_3_out, and_4_out, and_5_out, and_6_out, and_7_out, and_8_out, and_9_out,
       and_10_out, and_11_out, and_12_out, and_13_out, and_14_out, and_15_out, and_16_out, and_17_out,
       and_18_out, and_19_out, and_20_out, and_21_out, and_22_out, and_23_out, and_24_out, and_25_out,
       and_26_out, and_27_out, and_28_out, and_29_out, and_30_out, IR4, IR7, IR8, IR10, not_1_out, not_2_out,
       not_3_out, not_4_out, not_5_out, not_6_out, not_7_out, not_8_out, not_9_out, not_10_out, not_11_out,
       not_12_out, not_13_out, not_14_out, not_15_out, not_16_out, not_17_out, not_18_out, not_19_out,
       not_20_out, not_21_out, not_22_out, not_23_out, not_24_out, Opcode0, Opcode2, Opcode3, Opcode4,
       Opcode5, Opcode6, Opcode7, Opcode8, Opcode9, Opcode10, Opcode11, Opcode12, Opcode13, Opcode14,
       Opcode16, Opcode17, Opcode18, or_1_out, or_2_out, or_3_out, or_4_out, or_5_out, or_6_out, or_7_out,
       T1, T3, T4, T5, T6, Z;
  wire [2:0] DESTREG_2B_2;

  not not_1 (not_1_out, IR4);
  not not_2 (not_2_out, IR4);
  and and_1 (and_1_out, Opcode17, T6);
  not not_3 (not_3_out, Z);
  and and_2 (and_2_out, not_3_out, Opcode16);
  not not_4 (not_4_out, IR7);
  not not_5 (not_5_out, IR7);
  not not_6 (not_6_out, IR10);
  not not_7 (not_7_out, IR7);
  not not_8 (not_8_out, IR7);
  not not_9 (not_9_out, IR4);
  not not_10 (not_10_out, IR7);
  not not_11 (not_11_out, IR7);
  not not_12 (not_12_out, IR7);
  not not_13 (not_13_out, IR7);
  not not_14 (not_14_out, IR7);
  not not_15 (not_15_out, IR7);
  not not_16 (not_16_out, IR4);
  not not_17 (not_17_out, IR7);
  not not_18 (not_18_out, IR4);
  not not_19 (not_19_out, IR7);
  not not_20 (not_20_out, IR4);
  not not_21 (not_21_out, IR7);
  not not_22 (not_22_out, IR4);
  not not_23 (not_23_out, IR7);
  or or_1 (or_1_out, not_23_out, IR7);
  or or_2 (or_2_out, Opcode11, Opcode12, Opcode13);
  and and_3 (and_3_out, Opcode18, T4);
  and and_4 (and_4_out, Opcode4, T4);
  and and_5 (and_5_out, Opcode17, T5);
  and and_6 (and_6_out, Opcode18, T5);
  not not_24 (not_24_out, IR8);
  and and_7 (and_7_out, or_3_out, T4);
  and and_8 (and_8_out, T4, not_4_out, IR10, Opcode2);
  and and_9 (and_9_out, T4, not_5_out, not_6_out, Opcode2);
  and and_10 (and_10_out, T5, not_10_out, IR10, IR4, Opcode6);
  and and_11 (and_11_out, T4, IR7, IR10, Opcode7);
  and and_12 (and_12_out, T5, IR7, IR10, Opcode7);
  and and_13 (and_13_out, T4, not_11_out, IR10, Opcode7);
  and and_14 (and_14_out, T5, not_12_out, IR10, Opcode7);
  and and_15 (and_15_out, T4, IR7, IR10, Opcode8);
  and and_16 (and_16_out, T5, IR7, IR10, Opcode8);
  and and_17 (and_17_out, T5, or_1_out, IR10, or_2_out);
  and and_18 (and_18_out, T4, not_24_out, Opcode0);
  or or_3 (or_3_out, Opcode3, Opcode14, and_2_out);
  and and_19 (and_19_out, T4, IR10, Opcode2);
  and and_20 (and_20_out, T5, not_7_out, IR10, not_1_out, Opcode5);
  and and_21 (and_21_out, T5, IR7, IR10, not_2_out, Opcode5);
  and and_22 (and_22_out, T4, not_8_out, IR10, not_9_out, Opcode6);
  and and_23 (and_23_out, T4, not_13_out, IR10, Opcode8);
  and and_24 (and_24_out, T5, not_14_out, IR10, Opcode8);
  and and_25 (and_25_out, T4, not_15_out, IR10, not_16_out, Opcode9);
  and and_26 (and_26_out, T5, not_17_out, IR10, IR4, Opcode9);
  and and_27 (and_27_out, T5, IR7, IR10, not_18_out, Opcode9);
  and and_28 (and_28_out, T4, not_19_out, IR10, not_20_out, Opcode10);
  and and_29 (and_29_out, T5, not_21_out, IR10, IR4, Opcode10);
  and and_30 (and_30_out, T5, IR7, IR10, not_22_out, Opcode10);
  or or_4 (or_4_out, and_4_out, and_5_out, and_3_out);
  or or_5 (or_5_out, T1, T3, and_1_out, and_6_out);
  or or_6 (or_6_out, and_18_out, and_7_out);
  or or_7 (or_7_out, and_19_out, and_8_out, and_9_out, and_20_out, and_21_out, and_22_out, and_10_out, and_11_out, and_12_out, and_13_out, and_14_out, and_15_out, and_16_out, and_23_out, and_24_out, and_25_out, and_26_out, and_27_out, and_28_out, and_29_out, and_30_out, and_17_out);
  assign EN = or_5_out ? 3'b001 : 3'bz;  // Controlled_Buffer controlled_buffer_1
  assign EN = or_6_out ? 3'b010 : 3'bz;  // Controlled_Buffer controlled_buffer_2
  assign EN = or_7_out ? DESTREG_2B_2 : 3'bz;  // Controlled_Buffer controlled_buffer_3
  assign EN = or_4_out ? 3'b100 : 3'bz;  // Controlled_Buffer controlled_buffer_4
endmodule
