// Logisim project sequencer.circ as structural Verilog: 1 circuit, main circuit main
module main (
  input  CLK,
  input  [9:0] MAP,
  input  Z,
  output [5:0] MicroOp
);

  wire and_1_out, and_2_out, and_3_out, multiplexer_2_out, not_1_out, not_2_out, not_3_out;
  wire [1:0] or_1_out;
  wire [9:0] adder_1_out, main_1_output, main_2_output, multiplexer_1_out;
  wire [13:0] rom_1_data;

  not not_1 (not_1_out, or_1_out[1]);
  Adder #(.width(10)) adder_1 (.a(main_2_output), .b(10'h1), .out(adder_1_out));  // open: cin, cout
  _9_BIT_D_FLIP_FLOP_main main_1 (.CLK(CLK), .EN(and_3_out), .INPUT(adder_1_out), .OUTPUT(main_1_output));
  and and_1 (and_1_out, rom_1_data[11], or_1_out[1]);
  and and_2 (and_2_out, not_1_out, multiplexer_2_out);
  Multiplexer #(.select(2), .width(10)) multiplexer_1 (
    .in0(adder_1_out), .in1(rom_1_data[9:0]), .in2(main_1_output), .in3(MAP), .out(multiplexer_1_out),
    .sel(or_1_out));  // open: en
  or or_1 (or_1_out[0], and_1_out, and_2_out);
  not not_2 (not_2_out, Z);
  not not_3 (not_3_out, or_1_out[1]);
  and and_3 (and_3_out, rom_1_data[11], not_3_out, multiplexer_2_out);
  Multiplexer #(.select(2), .enable("false")) multiplexer_2 (
    .in0(1'b1), .in1(Z), .in2(not_2_out), .out(multiplexer_2_out), .sel(rom_1_data[13:12]));  // open: in3
  _9_BIT_D_FLIP_FLOP_main main_2 (.CLK(CLK), .INPUT(multiplexer_1_out), .OUTPUT(main_2_output));  // open: EN
  ROM #(.addrWidth(10), .dataWidth(20)) rom_1 (
    .addr(main_2_output), .data({MicroOp, rom_1_data[13:11], or_1_out[1], rom_1_data[9:0]}));  // open: sel

  // Notes on the sheet:
  //   SBR
  //   contents of rom_1 (hex, n*v repeats v):
  //   dc001 e4002 e0003 e4004 c00 c8000 c4000 505*0 4000 0 0 0 8000 11*0 c000 15*0 1c000 0 14000 5*0 18000
  //   0 10000 5*0 20231 28000 14*0 20241 28000 14*0 30000 34000 6*0 3c000 44000 40000 5*0 48000 50000 6*0
  //   4c000 54000 6*0 1c271 d0006 18273 d0006 4*0 14279 cc007 1027b cc007 4*0 1c281 dc006 18283 dc006 4*0
  //   14289 d8007 1028b d8007 4*0 58000 60000 68000 5*0 5c000 64000 68000 5*0 70000 78000 80000 5*0 74000
  //   7c000 84000 5*0 88000 0 90000 5*0 8c000 0 94000 5*0 98000 0 a0000 5*0 9c000 0 a4000 5*0 a8000 0
  //   b0000 5*0 ac000 0 b4000 5*0 b8000 15*0 12f2 0 b8000 13*0 ba302 0 b8000 13*0 bc311 28312 b8000 13*0
  //   2c321 c0000
endmodule
