// Logisim project tc.circ as structural Verilog: 1 circuit, main circuit main
module main (
  input  in_1,
  input  in_2,
  input  in_3,
  input  in_4
);

  wire and_1_out, and_2_out, and_3_out, and_4_out, and_5_out, and_6_out, IR4, IR7, not_1_out, not_2_out,
       not_3_out, not_4_out, Opcode10, Opcode12, Opcode13, Opcode14, Opcode15, Opcode16, Opcode17, Opcode18,
       or_1_out, or_2_out, or_3_out, T4, T5, T6;

  not not_1 (not_1_out, IR4);
  not not_2 (not_2_out, IR7);
  not not_3 (not_3_out, IR7);
  not not_4 (not_4_out, IR4);
  or or_1 (or_1_out, Opcode12, Opcode13, Opcode18);
  or or_2 (or_2_out, Opcode14, Opcode15, Opcode16);
  and and_1 (and_1_out, not_1_out, not_2_out, Opcode10, T4);
  and and_2 (and_2_out, IR4, not_3_out, Opcode10, T5);
  and and_3 (and_3_out, IR7, not_4_out, Opcode10, T5);
  and and_4 (and_4_out, or_1_out, T5);
  and and_5 (and_5_out, or_2_out, T4);
  and and_6 (and_6_out, Opcode17, T6);
  or or_3 (or_3_out, and_1_out, and_2_out, and_3_out, and_4_out, and_5_out, and_6_out);
endmodule
