// Logisim project timeclear10-18.circ as structural Verilog: 1 circuit, main circuit main
module main (
  input  in_1,
  input  in_2,
  input  in_3,
  input  in_4
);

  wire and_1_out, and_2_out, and_3_out, and_4_out, and_5_out, IR4, IR7, IR8, not_1_out, not_2_out, not_3_out,
       Opcode0, Opcode1, Opcode2, Opcode3, Opcode4, Opcode5, Opcode6, Opcode7, Opcode8, Opcode9, Opcode10,
       Opcode12, Opcode13, Opcode14, Opcode15, Opcode16, Opcode17, Opcode18, or_1_out, or_2_out, or_3_out,
       or_4_out, or_5_out, or_6_out, or_7_out, T4, T5, T6, xor_1_out;

  or or_1 (or_1_out, Opcode10, Opcode6, Opcode9);
  or or_2 (or_2_out, Opcode10, Opcode6, Opcode9);
  or or_3 (or_3_out, Opcode14, Opcode2, Opcode3, Opcode15, Opcode16);
  not not_1 (not_1_out, IR4);
  not not_2 (not_2_out, IR7);
  xor xor_1 (xor_1_out, IR4, IR7);
  or or_4 (or_4_out, Opcode12, Opcode1, Opcode4, Opcode5, Opcode13, Opcode18);
  or or_5 (or_5_out, Opcode7, Opcode17, Opcode8);
  not not_3 (not_3_out, IR8);
  or or_6 (or_6_out, Opcode1, Opcode4);
  and and_1 (and_1_out, or_3_out, T4);
  and and_2 (and_2_out, or_5_out, T6);
  and and_3 (and_3_out, not_1_out, not_2_out, or_2_out, T4);
  and and_4 (and_4_out, xor_1_out, or_1_out, T5);
  and and_5 (and_5_out, or_4_out, T5);
  // AND_Gate and_6 has open pins: in0=not_3_out, in2=Opcode0, in4=T5, out=open
  // AND_Gate and_7 has open pins: in0=IR8, in2=Opcode0, in4=T4, out=open
  // AND_Gate and_8 has open pins: in0=or_6_out, in4=T5, out=open
  or or_7 (or_7_out, and_3_out, and_4_out, and_5_out, and_1_out, and_2_out);
endmodule
