// Logisim project verda.circ as structural Verilog: 1 circuit, main circuit main
module main (
  output [1:0] MuxBSel,
  output Read,
  output Load,
  output MuxASelEnable,
  output [1:0] MuxASel,
  output EnableRam,
  output MuxCSel,
  output MuxBSelEnable,
  output Enable_2C,
  output MuxCSelEnable,
  output L_H,
  output [1:0] FunSel_2C,
  output [1:0] MuxASel_2
);

  wire and_1_out, and_2_out, and_3_out, and_4_out, and_5_out, and_6_out, and_7_out, and_8_out, and_9_out,
       and_10_out, and_11_out, and_12_out, and_13_out, and_14_out, and_15_out, and_16_out, and_17_out,
       and_18_out, and_19_out, and_20_out, and_21_out, and_22_out, and_23_out, and_24_out, and_25_out,
       and_26_out, and_27_out, and_28_out, and_29_out, and_30_out, and_31_out, and_32_out, and_33_out,
       and_34_out, and_35_out, and_36_out, and_37_out, and_38_out, and_39_out, and_40_out, and_41_out,
       and_42_out, and_43_out, and_44_out, and_45_out, and_46_out, IR4, IR7, IR8, IR10, not_2_out, not_3_out,
       not_4_out, not_5_out, not_6_out, not_7_out, not_8_out, not_9_out, not_10_out, not_11_out, not_12_out,
       not_13_out, not_14_out, not_15_out, not_16_out, not_17_out, not_18_out, not_19_out, not_20_out,
       not_21_out, not_22_out, not_23_out, not_24_out, not_25_out, not_26_out, not_27_out, not_28_out,
       not_29_out, not_30_out, not_31_out, not_32_out, not_33_out, not_34_out, not_35_out, not_36_out,
       not_37_out, not_38_out, not_39_out, not_40_out, not_41_out, not_42_out, not_43_out, not_44_out,
       Opcode0, Opcode1, Opcode2, Opcode3, Opcode4, Opcode5, Opcode6, Opcode7, Opcode8, Opcode9, Opcode10,
       Opcode11, Opcode12, Opcode13, Opcode14, Opcode15, Opcode16, Opcode17, Opcode18, Opcode_2_7,
       Opcode_2_7_8, Opcode_2_7_8_11_12_13, Opcode_9_10, Opcode_9_10_17, Opcode_11_12_13, or_1_out, or_9_out,
       or_10_out, or_12_out, or_13_out, or_14_out, or_15_out, or_16_out, or_17_out, or_18_out, or_19_out,
       or_21_out, or_22_out, or_24_out, or_25_out, or_26_out, or_27_out, or_28_out, T0, T2, T4, T5, T6, T7,
       undriven, Z;

  and and_1 (and_1_out, T4, Opcode17);
  and and_2 (and_2_out, T4, Opcode3);
  and and_3 (and_3_out, T5, Opcode0);
  and and_4 (and_4_out, T5, undriven);
  and and_5 (and_5_out, T5, Opcode18);
  assign L_H = T0 ? 1'b0 : 1'bz;  // Controlled_Buffer controlled_buffer_1
  assign L_H = T2 ? 1'b1 : 1'bz;  // Controlled_Buffer controlled_buffer_2
  or or_1 (or_1_out, T0, T2);
  or or_2 (Enable_2C, T0, T2);
  assign FunSel_2C = or_1_out ? 2'b11 : 2'bz;  // Controlled_Buffer controlled_buffer_3
  or or_3 (Opcode_2_7_8_11_12_13, Opcode2, Opcode7, Opcode8, Opcode11, Opcode12, Opcode13);
  or or_4 (Opcode_9_10_17, Opcode9, Opcode10, Opcode17);
  or or_5 (Opcode_11_12_13, Opcode11, Opcode12, Opcode13);
  or or_6 (Opcode_2_7, Opcode2, Opcode7);
  or or_7 (Opcode_2_7_8, Opcode2, Opcode7, Opcode8);
  or or_8 (Opcode_9_10, Opcode9, Opcode10);
  or or_9 (or_9_out, and_1_out, and_2_out);
  assign Read = or_9_out ? 1'b0 : 1'bz;  // Controlled_Buffer controlled_buffer_4
  assign Read = or_10_out ? 1'b1 : 1'bz;  // Controlled_Buffer controlled_buffer_5
  or or_10 (or_10_out, T0, T2, and_3_out, and_4_out, and_5_out);
  or or_11 (EnableRam, or_9_out, or_10_out);
  not not_1 (Load, Read);
  or or_12 (or_12_out, Opcode5, Opcode6);
  or or_13 (or_13_out, Opcode_9_10, Opcode6);
  not not_2 (not_2_out, IR4);
  not not_3 (not_3_out, IR4);
  not not_4 (not_4_out, IR10);
  not not_5 (not_5_out, IR10);
  not not_6 (not_6_out, IR7);
  not not_7 (not_7_out, IR10);
  not not_8 (not_8_out, IR4);
  not not_9 (not_9_out, IR10);
  or or_14 (or_14_out, T4, T5, T6);
  not not_10 (not_10_out, IR4);
  not not_11 (not_11_out, IR7);
  or or_15 (or_15_out, Opcode5, Opcode6);
  not not_12 (not_12_out, IR7);
  not not_13 (not_13_out, IR10);
  not not_14 (not_14_out, IR7);
  not not_15 (not_15_out, IR10);
  or or_16 (or_16_out, Opcode5, Opcode8);
  not not_16 (not_16_out, IR4);
  not not_17 (not_17_out, IR7);
  not not_18 (not_18_out, IR10);
  not not_19 (not_19_out, IR7);
  not not_20 (not_20_out, IR10);
  not not_21 (not_21_out, IR7);
  not not_22 (not_22_out, IR10);
  and and_6 (and_6_out, T5, not_4_out, Opcode_11_12_13);
  not not_23 (not_23_out, IR8);
  not not_24 (not_24_out, IR8);
  and and_7 (and_7_out, IR7, Opcode_2_7_8_11_12_13, T4);
  and and_8 (and_8_out, IR10, IR7, not_10_out, Opcode5, T4);
  and and_9 (and_9_out, T4, not_12_out, not_13_out, Opcode_2_7);
  and and_10 (and_10_out, T5, not_14_out, not_15_out, or_16_out);
  and and_11 (and_11_out, T4, not_16_out, not_17_out, not_18_out, or_13_out);
  and and_12 (and_12_out, T5, IR4, not_19_out, not_20_out, Opcode_9_10);
  and and_13 (and_13_out, T5, not_2_out, not_21_out, IR10, Opcode9);
  and and_14 (and_14_out, T5, not_3_out, IR7, not_22_out, Opcode10);
  and and_15 (and_15_out, T5, not_23_out, Opcode0);
  and and_16 (and_16_out, T4, not_24_out, Opcode0);
  and and_17 (and_17_out, T5, Opcode4);
  and and_18 (and_18_out, T4, Opcode_9_10_17);
  and and_19 (and_19_out, not_5_out, not_6_out, IR4, or_12_out, T4);
  and and_20 (and_20_out, not_7_out, IR7, not_8_out, Opcode5, T4);
  and and_21 (and_21_out, not_9_out, IR7, IR4, Opcode5, or_14_out);
  and and_22 (and_22_out, IR10, not_11_out, IR4, T4, or_15_out);
  or or_17 (or_17_out, and_15_out, and_16_out, and_17_out);
  or or_18 (or_18_out, and_7_out, and_18_out, and_19_out, and_20_out, and_21_out, and_8_out, and_22_out);
  or or_19 (or_19_out, and_9_out, and_10_out, and_11_out, and_12_out, and_13_out, and_14_out, and_6_out);
  or or_20 (MuxASelEnable, or_19_out, or_17_out, or_18_out);
  assign MuxASel = or_17_out ? 2'b01 : 2'bz;  // Controlled_Buffer controlled_buffer_6
  assign MuxASel = or_18_out ? 2'b10 : 2'bz;  // Controlled_Buffer controlled_buffer_7
  assign MuxASel = or_19_out ? 2'b11 : 2'bz;  // Controlled_Buffer controlled_buffer_8
  not not_25 (not_25_out, IR4);
  not not_26 (not_26_out, IR7);
  not not_27 (not_27_out, IR10);
  not not_28 (not_28_out, IR4);
  not not_29 (not_29_out, IR7);
  not not_30 (not_30_out, IR7);
  not not_31 (not_31_out, Z);
  not not_32 (not_32_out, IR8);
  and and_23 (and_23_out, T5, Opcode18);
  and and_24 (and_24_out, T4, not_26_out, not_27_out, Opcode2);
  and and_25 (and_25_out, T4, not_28_out, not_29_out, IR10, Opcode_9_10);
  and and_26 (and_26_out, T5, IR4, not_30_out, IR10, Opcode_9_10);
  and and_27 (and_27_out, T5, not_25_out, IR7, IR10, Opcode_9_10);
  and and_28 (and_28_out, T5, IR10, Opcode_11_12_13);
  and and_29 (and_29_out, T5, not_31_out, Opcode16);
  and and_30 (and_30_out, T4, Opcode15);
  and and_31 (and_31_out, T4, Opcode14);
  and and_32 (and_32_out, T7, Opcode17);
  and and_33 (and_33_out, T4, not_32_out, Opcode0);
  and and_34 (and_34_out, T4, IR10, Opcode_2_7_8);
  or or_21 (or_21_out, and_29_out, and_30_out, and_31_out, and_32_out, and_33_out);
  or or_22 (or_22_out, and_34_out, and_24_out, and_25_out, and_26_out, and_27_out, and_28_out);
  assign MuxBSel = or_21_out ? 2'b01 : 2'bz;  // Controlled_Buffer controlled_buffer_9
  assign MuxBSel = and_23_out ? 2'b10 : 2'bz;  // Controlled_Buffer controlled_buffer_10
  assign MuxBSel = or_22_out ? 2'b11 : 2'bz;  // Controlled_Buffer controlled_buffer_11
  or or_23 (MuxBSelEnable, or_21_out, and_23_out, or_22_out);
  not not_33 (not_33_out, IR7);
  not not_34 (not_34_out, IR4);
  not not_35 (not_35_out, IR7);
  not not_36 (not_36_out, IR10);
  not not_37 (not_37_out, IR4);
  not not_38 (not_38_out, IR10);
  or or_24 (or_24_out, Opcode5, Opcode6);
  not not_39 (not_39_out, IR10);
  not not_40 (not_40_out, IR7);
  not not_41 (not_41_out, IR7);
  not not_42 (not_42_out, IR4);
  not not_43 (not_43_out, IR4);
  not not_44 (not_44_out, IR7);
  or or_25 (or_25_out, Opcode5, Opcode6);
  and and_35 (and_35_out, T4, Opcode_2_7_8, IR7, IR10);
  and and_36 (and_36_out, T4, Opcode_9_10, IR4, not_33_out);
  and and_37 (and_37_out, T4, Opcode_9_10, IR7, not_34_out);
  and and_38 (and_38_out, T4, Opcode17);
  and and_39 (and_39_out, T4, IR4, not_35_out, not_36_out, Opcode5);
  and and_40 (and_40_out, T4, IR7, not_37_out, not_38_out, or_24_out);
  and and_41 (and_41_out, T5, IR4, IR7, not_39_out, Opcode5);
  or or_26 (or_26_out, Opcode5, Opcode6);
  and and_42 (and_42_out, T4, Opcode1);
  and and_43 (and_43_out, T4, Opcode_9_10, not_41_out, not_42_out);
  and and_44 (and_44_out, T4, Opcode_11_12_13);
  and and_45 (and_45_out, T4, not_43_out, not_44_out, or_25_out);
  and and_46 (and_46_out, T4, IR4, not_40_out, IR10, or_26_out);
  or or_27 (or_27_out, and_35_out, and_36_out, and_37_out, and_38_out, and_39_out, and_40_out, and_41_out, and_46_out);
  or or_28 (or_28_out, and_42_out, and_43_out, and_44_out, and_45_out);
  or or_29 (MuxCSelEnable, or_27_out, or_28_out);
  assign MuxCSel = or_27_out ? 1'b0 : 1'bz;  // Controlled_Buffer controlled_buffer_12
  assign MuxCSel = or_28_out ? 1'b1 : 1'bz;  // Controlled_Buffer controlled_buffer_13
endmodule
